// Logisim project CPU2908C7.circ as structural Verilog: 25 circuits, main circuit PC-2908C
module PC_2908C (
);

  wire Reset_out;
  wire [7:0] keyboard_1_data;
  wire [11:0] system_1_console_out;

  Button Reset (.out(Reset_out));
  System system_1 (.ResetIn(Reset_out), .Console_OUT(system_1_console_out), .Console_IN(keyboard_1_data));
  TTY #(.rows(25), .cols(80)) tty_1 (
    .data(system_1_console_out[6:0]), .clk(system_1_console_out[7]), .we(system_1_console_out[8]),
    .clr(system_1_console_out[9]));
  Keyboard keyboard_1 (
    .clk(system_1_console_out[7]), .re(system_1_console_out[10]), .clr(system_1_console_out[11]),
    .avail(keyboard_1_data[7]), .data(keyboard_1_data[6:0]));

  // Notes on the sheet:
  //   Key Input
endmodule

module System (
  input  ResetIn,
  input  [7:0] Console_IN,
  output [11:0] Console_OUT
);

  wire CLK, decoder_1_out0, decoder_1_out1, decoder_1_out2, decoder_1_out3, equal14_1_y, equal14_2_y, IRQ,
       n2908c_core_1_irqa, n2908c_core_1_read, n2908c_core_1_s0, n2908c_core_1_s1, n2908c_core_1_write,
       not_1_out, not_2_out, not_3_out, or_1_out, or_2_out;
  wire [6:0] n2908c_core_1_dataout;
  wire [7:0] register_1_q, xorshift_1_rnd;
  wire [7:7] n2908c_core_1_dataout_2;
  wire [9:0] counter_1_q;
  wire [15:0] n2908c_core_1_addressout;

  Clock Clock (.out(CLK));
  Counter #(.width(10), .max('h3ff)) counter_1 (.Q(counter_1_q), .clk(CLK));  // open: load, D, count, carry, clr
  Pull_Resistor #(.pull(1)) pull_resistor_1 (.node(IRQ));
  LED led_1 (.in(counter_1_q[8]));
  _2908C_CORE u_2908c_core_1 (
    .Reset(ResetIn), .DataOut({n2908c_core_1_dataout_2[7], n2908c_core_1_dataout}),
    .DataIn({n2908c_core_1_dataout_2[7], n2908c_core_1_dataout}), .Read(n2908c_core_1_read),
    .AddressOut(n2908c_core_1_addressout), .CLK(CLK), .nIRQ(counter_1_q[8]), .Write(n2908c_core_1_write),
    .IRQA(n2908c_core_1_irqa), .nTSC(IRQ), .MRDY(IRQ), .S0(n2908c_core_1_s0), .S1(n2908c_core_1_s1));  // open: IRQH, LOCK, VMA
  // Probe on {n2908c_core_1_dataout_2[7], n2908c_core_1_dataout}
  // Probe on n2908c_core_1_addressout
  Pull_Resistor #(.pull(1)) pull_resistor_2 (.node(n2908c_core_1_write));
  Pull_Resistor #(.pull(1)) pull_resistor_3 (.node(n2908c_core_1_read));
  Pull_Resistor #(.pull(1)) pull_resistor_4 (.node(n2908c_core_1_irqa));
  Pull_Resistor #(.pull(1)) pull_resistor_5 (.node({n2908c_core_1_dataout_2[7], n2908c_core_1_dataout}));
  Pull_Resistor pull_resistor_6 (.node(n2908c_core_1_addressout));
  not not_1 (not_1_out, n2908c_core_1_write);
  not not_2 (not_2_out, or_1_out);
  or or_1 (or_1_out, equal14_1_y, equal14_2_y);
  Decoder #(.select(2), .disabled(0)) decoder_1 (
    .out0(decoder_1_out0), .out1(decoder_1_out1), .out2(decoder_1_out2), .out3(decoder_1_out3),
    .sel(n2908c_core_1_addressout[15:14]), .en(not_2_out));
  Equal14 equal14_1 (.In0(n2908c_core_1_addressout[15:2]), .In1(14'h3f84), .Y(equal14_1_y));
  assign {n2908c_core_1_dataout_2[7], n2908c_core_1_dataout} = equal14_2_y ? xorshift_1_rnd : 8'bz;  // Controlled_Buffer controlled_buffer_1
  Equal14 equal14_2 (.In0(n2908c_core_1_addressout[15:2]), .In1(14'h3fa1), .Y(equal14_2_y));
  // Probe on xorshift_1_rnd
  XORSHIFT xorshift_1 (.RND(xorshift_1_rnd), .CLK(CLK));
  and and_1 (Console_OUT[8], equal14_1_y, not_1_out);
  and and_2 (Console_OUT[10], equal14_1_y, n2908c_core_1_read);
  assign {n2908c_core_1_dataout_2[7], n2908c_core_1_dataout} = Console_OUT[10] ? register_1_q : 8'bz;  // Controlled_Buffer controlled_buffer_2
  ROM #(.addrWidth(14)) rom_1 (
    .addr(n2908c_core_1_addressout[13:0]), .data({n2908c_core_1_dataout_2[7], n2908c_core_1_dataout}),
    .sel(decoder_1_out0));
  assign Console_OUT[6:0] = Console_OUT[8] ? n2908c_core_1_dataout : 7'bz;  // Controlled_Buffer controlled_buffer_3
  or or_2 (or_2_out, Console_OUT[8], Console_OUT[10]);
  not not_3 (not_3_out, or_2_out);
  not not_4 (Console_OUT[7], not_3_out);
  RAM #(.addrWidth(14)) ram_1 (
    .addr(n2908c_core_1_addressout[13:0]), .data({n2908c_core_1_dataout_2[7], n2908c_core_1_dataout}),
    .sel(decoder_1_out1), .clk(not_1_out), .ld(n2908c_core_1_read), .clr(1'b0));
  Register register_1 (.D(Console_IN), .en(Console_OUT[10]), .Q(register_1_q), .clk(Console_OUT[10]), .clr(ResetIn));
  RAM #(.addrWidth(14)) ram_2 (
    .addr(n2908c_core_1_addressout[13:0]), .data({n2908c_core_1_dataout_2[7], n2908c_core_1_dataout}),
    .sel(decoder_1_out2), .clk(not_1_out), .ld(n2908c_core_1_read), .clr(1'b0));
  RAM #(.addrWidth(14)) ram_3 (
    .addr(n2908c_core_1_addressout[13:0]), .data({n2908c_core_1_dataout_2[7], n2908c_core_1_dataout}),
    .sel(decoder_1_out3), .clk(not_1_out), .ld(n2908c_core_1_read), .clr(1'b0));

  assign {Console_OUT[11], Console_OUT[9]} = {2{ResetIn}};

  // Other names for the same wires on the sheet: Reset = ResetIn

  // Notes on the sheet:
  //   ROM0
  //   RAM0
  //   contents of rom_1 (hex, n*v repeats v):
  //   60 68 0 7b 0 7d 1f 0 5 bf e5 4 d7 fe 2 0 ee fe 7c 0 f 0 a5 8 e5 fb d6 9 fe e9 ff 48 65 6c 6c 6f 0 6e
  //   48 65 6c 6c 6f 43*0 76 1199*0 76 2553*0 f8 aa 8478*0 6e
  //   RAM1
  //   RAM2
endmodule

module XORSHIFT (
  input  CLK,
  output [7:0] RND
);

  wire Initialize, not_1_out, not_2_out, not_3_out, not_4_out, not_5_out, not_6_out, not_7_out, not_8_out,
       not_9_out, not_10_out, not_11_out, not_12_out, not_13_out, not_14_out, not_15_out, not_16_out;
  wire [7:0] T_q;
  wire [12:0] W_q_2;
  wire [18:0] W_q;
  wire [23:0] T_q_2;
  wire [31:0] multiplexer_1_out, multiplexer_2_out, multiplexer_3_out, multiplexer_4_out, X_q, xor_1_out,
       xor_2_out, xor_3_out, Y_q, Z_q;
  wire [31:8] xor_4_out;

  Register #(.width(1)) register_1 (.D(1'b1), .en(1'b1), .Q(Initialize), .clk(CLK), .clr(1'b0));
  Multiplexer #(.width(32)) multiplexer_1 (
    .in0(32'h1f123bb5), .in1({W_q_2, W_q}), .out(multiplexer_1_out), .sel(Initialize), .en(1'b1));
  not not_1 (not_1_out, not_2_out);
  not not_2 (not_2_out, CLK);
  Register #(.width(32)) Z (.D(multiplexer_1_out), .en(1'b1), .Q(Z_q), .clk(not_1_out), .clr(1'b0));
  Multiplexer #(.width(32)) multiplexer_2 (
    .in0(32'h159a55e5), .in1(Z_q), .out(multiplexer_2_out), .sel(Initialize), .en(1'b1));
  Register #(.width(32), .trigger("falling")) Y (
    .D(multiplexer_2_out), .en(1'b1), .Q(Y_q), .clk(not_3_out), .clr(1'b0));
  not not_3 (not_3_out, CLK);
  Multiplexer #(.width(32)) multiplexer_3 (
    .in0(32'h75bcd15), .in1(Y_q), .out(multiplexer_3_out), .sel(Initialize), .en(1'b1));
  Register #(.width(32)) X (.D(multiplexer_3_out), .en(1'b1), .Q(X_q), .clk(CLK), .clr(1'b0));
  assign xor_1_out = X_q ^ {X_q[20:0], {11{1'b0}}};  // XOR_Gate xor_1, 32 bits wide
  not not_4 (not_4_out, not_5_out);
  not not_5 (not_5_out, not_6_out);
  not not_6 (not_6_out, not_10_out);
  not not_7 (not_7_out, not_4_out);
  not not_8 (not_8_out, not_9_out);
  not not_9 (not_9_out, not_11_out);
  not not_10 (not_10_out, not_8_out);
  not not_11 (not_11_out, not_13_out);
  not not_12 (not_12_out, CLK);
  not not_13 (not_13_out, not_12_out);
  Register #(.width(32)) T (.D(xor_1_out), .en(1'b1), .Q({T_q_2, T_q}), .clk(not_7_out), .clr(1'b0));
  Multiplexer #(.width(32)) multiplexer_4 (
    .in0(32'h5491333), .in1({xor_4_out, RND}), .out(multiplexer_4_out), .sel(Initialize), .en(1'b1));
  assign xor_2_out = {T_q_2, T_q} ^ {{8{1'b0}}, T_q_2};  // XOR_Gate xor_2, 32 bits wide
  not not_14 (not_14_out, CLK);
  not not_15 (not_15_out, not_14_out);
  Register #(.width(32), .trigger("falling")) W (
    .D(multiplexer_4_out), .en(1'b1), .Q({W_q_2, W_q}), .clk(not_16_out), .clr(1'b0));
  not not_16 (not_16_out, not_15_out);
  assign xor_3_out = {W_q_2, W_q} ^ {{19{1'b0}}, W_q_2};  // XOR_Gate xor_3, 32 bits wide
  // Probe on {xor_4_out, RND}
  assign {xor_4_out, RND} = xor_3_out ^ xor_2_out;  // XOR_Gate xor_4, 32 bits wide

  // Notes on the sheet:
  //   負論理：シミュレーションがリセットされたあと最初の
  //   クロックでレジスタに初期値をロードする
endmodule

module Equal14 (
  input  [13:0] In0,
  input  [13:0] In1,
  output Y
);

  wire [13:0] not_1_out, xor_1_out;

  assign not_1_out = ~xor_1_out;  // NOT_Gate not_1, 14 bits wide
  assign xor_1_out = In0 ^ In1;  // XOR_Gate xor_1, 14 bits wide
  and and_1 (Y, not_1_out[0], not_1_out[1], not_1_out[2], not_1_out[3], not_1_out[4], not_1_out[5], not_1_out[6], not_1_out[7], not_1_out[8], not_1_out[9], not_1_out[10], not_1_out[11], not_1_out[12], not_1_out[13]);
endmodule

module _2908C_CORE (
  input  nTSC,
  input  nIRQ,
  input  [7:0] DataIn,
  input  MRDY,
  input  CLK,
  input  Reset,
  output [7:0] DataOut,
  output [15:0] AddressOut,
  output VMA,
  output IRQA,
  output Write,
  output Read,
  output IRQH,
  output LOCK,
  output S0,
  output S1
);

  wire and_2_out, and_3_out, and_4_out, clk_gen_1_wait, d_ff_1_q, d_ff_2_qn, d_ff_3_qn, d_ff_4_qn, d_ff_5_qn,
       d_ff_6_qn, E, executer_1_traceflag, MPI, not_1_out, not_2_out, not_3_out, not_4_out, not_5_out,
       not_6_out, not_7_out, nRST, nTSC_t, Q, sequencer_1_jump_op, sequencer_1_ndo_jump,
       sequencer_1_stateclock, sequencer_1_stepctrl, sequencer_1_stepupdate;
  wire [4:0] sequencer_1_exbuscontrol;
  wire [7:0] executer_1_dataout, executer_1_flagregisterout, register_1_q, sequencer_1_dataout;
  wire [11:0] sequencer_1_step;
  wire [15:0] executer_1_addrout, register_2_q;
  wire [23:0] sequencer_1_registercontrol;

  not not_1 (not_1_out, nRST);
  and and_1 (nTSC_t, nTSC, nRST);
  D_Flip_Flop d_ff_1 (.clk(Q), .D(MPI), .Q(d_ff_1_q), .reset(not_1_out));  // open: Qn, preset, en
  CLK_GEN clk_gen_1 (.nMRDY(MRDY), .CLK(CLK), .Reset(Reset), .Q(Q), .E(E), .WAIT(clk_gen_1_wait), .nRST(nRST));
  D_Flip_Flop d_ff_2 (.clk(d_ff_1_q), .D(d_ff_2_qn), .Q(LOCK), .Qn(d_ff_2_qn), .reset(not_1_out));  // open: preset, en
  Executer executer_1 (
    .DataOut(executer_1_dataout), .FlagRegisterOut(executer_1_flagregisterout), .Q(Q), .E(E),
    .AddrOut(executer_1_addrout), .DataIn(sequencer_1_dataout), .Reset(nRST),
    .RegisterCtrl(sequencer_1_registercontrol), .STEP(sequencer_1_step), .TraceFlag(executer_1_traceflag));
  Sequencer sequencer_1 (
    .FlagIn(executer_1_flagregisterout), .Q(Q), .E(E), .IRQ(nIRQ), .nReset(nRST), .DataIn(DataIn),
    .RegisterControl(sequencer_1_registercontrol), .ExBusControl(sequencer_1_exbuscontrol),
    .STEP(sequencer_1_step), .DataOut(sequencer_1_dataout), .IQRH(IRQH), .S1(S1), .S0(S0),
    .StepUpdate(sequencer_1_stepupdate), .JUMP_OP(sequencer_1_jump_op), .nDO_JUMP(sequencer_1_ndo_jump),
    .StateClock(sequencer_1_stateclock), .StepCtrl(sequencer_1_stepctrl), .TraceFlag(executer_1_traceflag));  // open: EX, Set_μROM_Address
  not not_2 (not_2_out, Q);
  Register register_1 (
    .D(executer_1_dataout), .en(sequencer_1_exbuscontrol[2]), .Q(register_1_q), .clk(E));  // open: clr
  Register #(.width(16)) register_2 (
    .D(executer_1_addrout), .en(sequencer_1_exbuscontrol[3]), .Q(register_2_q), .clk(E));  // open: clr
  or or_1 (VMA, sequencer_1_exbuscontrol[1], sequencer_1_exbuscontrol[0]);
  and and_2 (and_2_out, sequencer_1_exbuscontrol[1], sequencer_1_exbuscontrol[0]);
  and and_3 (and_3_out, sequencer_1_exbuscontrol[1], ~sequencer_1_exbuscontrol[0]);  // AND_Gate
  and and_4 (and_4_out, sequencer_1_exbuscontrol[0], ~sequencer_1_exbuscontrol[1]);  // AND_Gate
  not not_3 (not_3_out, nRST);
  assign AddressOut = nTSC_t ? register_2_q : 16'bz;  // Controlled_Buffer controlled_buffer_1
  D_Flip_Flop d_ff_3 (.clk(not_2_out), .D(and_3_out), .Qn(d_ff_3_qn), .reset(not_3_out));  // open: Q, preset, en
  not not_4 (not_4_out, d_ff_3_qn);
  D_Flip_Flop d_ff_4 (.clk(E), .D(and_2_out), .Qn(d_ff_4_qn), .reset(not_3_out));  // open: Q, preset, en
  not not_5 (not_5_out, d_ff_4_qn);
  D_Flip_Flop d_ff_5 (.clk(E), .D(and_3_out), .Qn(d_ff_5_qn), .reset(not_3_out));  // open: Q, preset, en
  not not_6 (not_6_out, d_ff_5_qn);
  D_Flip_Flop d_ff_6 (.clk(E), .D(and_4_out), .Qn(d_ff_6_qn), .reset(not_3_out));  // open: Q, preset, en
  not not_7 (not_7_out, d_ff_6_qn);
  assign DataOut = not_4_out ? register_1_q : 8'bz;  // Controlled_Buffer controlled_buffer_2
  assign Write = nTSC_t ? not_6_out : 1'bz;  // Controlled_Buffer controlled_buffer_3
  assign Read = nTSC_t ? not_7_out : 1'bz;  // Controlled_Buffer controlled_buffer_4
  assign IRQA = nTSC_t ? not_5_out : 1'bz;  // Controlled_Buffer controlled_buffer_5

  // Notes on the sheet:
  //   Reset: pull=up
  //   DataBus
  //   DataBus
  //   AddressBus
endmodule

module CLK_GEN (
  input  nMRDY,
  input  CLK,
  input  Reset,
  output Q,
  output E,
  output WAIT,
  output nRST
);

  wire and_1_out, d_ff_1_q, d_ff_1_qn, d_ff_2_q, d_ff_3_q, d_ff_4_q, d_ff_5_qn, nand_1_out, nor_1_out,
       not_1_out, not_2_out, not_3_out, not_4_out, not_5_out, not_6_out, not_7_out, not_8_out, not_9_out,
       PowerOnReset_q;

  not not_1 (not_1_out, nMRDY);
  not not_2 (not_2_out, CLK);
  not not_3 (not_3_out, Reset);
  D_Flip_Flop d_ff_1 (.clk(not_2_out), .D(1'b0), .Q(d_ff_1_q), .Qn(d_ff_1_qn), .preset(not_4_out));  // open: en, reset
  not not_4 (not_4_out, and_1_out);
  D_Flip_Flop PowerOnReset (.clk(not_2_out), .D(1'b1), .Q(PowerOnReset_q));  // open: Qn, preset, en, reset
  nand nand_1 (nand_1_out, ~Q, not_1_out, E);  // NAND_Gate
  D_Flip_Flop d_ff_2 (.clk(not_2_out), .D(d_ff_1_q), .Q(d_ff_2_q), .preset(not_6_out));  // open: Qn, en, reset
  not not_5 (not_5_out, and_1_out);
  not not_6 (not_6_out, and_1_out);
  and and_1 (and_1_out, not_3_out, PowerOnReset_q);
  D_Flip_Flop d_ff_3 (.clk(not_2_out), .D(nand_1_out), .Q(d_ff_3_q), .preset(d_ff_4_q));  // open: Qn, en, reset
  not not_7 (not_7_out, not_2_out);
  D_Flip_Flop d_ff_4 (.clk(not_2_out), .D(d_ff_2_q), .Q(d_ff_4_q), .preset(not_5_out));  // open: Qn, en, reset
  nor nor_1 (nor_1_out, d_ff_4_q, ~d_ff_3_q);  // NOR_Gate
  D_Flip_Flop d_ff_5 (.clk(not_7_out), .D(Q), .Q(E), .Qn(d_ff_5_qn), .preset(not_8_out));  // open: en, reset
  not not_8 (not_8_out, d_ff_3_q);
  D_Flip_Flop d_ff_6 (.clk(not_7_out), .D(d_ff_5_qn), .Q(Q), .reset(not_9_out));  // open: Qn, preset, en
  not not_9 (not_9_out, nor_1_out);
  not not_10 (WAIT, d_ff_3_q);
  not not_11 (nRST, d_ff_4_q);

  // Notes on the sheet:
  //   LogiSimのシミュレーションリセット対応
endmodule

module Sequencer (
  input  [7:0] DataIn,
  input  nReset,
  input  Q,
  input  E,
  input  IRQ,
  input  TraceFlag,
  input  [7:0] FlagIn,
  output [11:0] STEP,
  output [23:0] RegisterControl,
  output StepCtrl,
  output \Set_μROM_Address ,
  output [1:0] EX,
  output StepUpdate,
  output [4:0] ExBusControl,
  output [7:0] DataOut,
  output StateClock,
  output S1,
  output S0,
  output JUMP_OP,
  output IQRH,
  output nDO_JUMP
);

  wire and_2_out, and_3_out, and_4_out, Bit0_qn, Bit1_qn, IRQ_t, JG, JL, multiplexer_3_out, nE, not_5_out,
       not_6_out, not_7_out, not_8_out, not_9_out, not_10_out, not_11_out, not_12_out, not_13_out, nQ,
       or_2_out, or_3_out, U11B_out, U12C_out, U13A_out, U13B_out, U14A_out, U14B_out, U15B_out, U15C_out,
       U20A_out, U21A_out;
  wire [0:0] not_1_out;
  wire [3:0] multiplexer_1_out;
  wire [7:0] HCT574_q, multiplexer_2_out;
  wire [17:12] and_1_out;
  wire [30:0] urom_b_1_ctrlsignal;
  wire [31:31] Ctrl_Signal_q;

  not not_1 (not_1_out[0], nDO_JUMP);
  not not_2 (nQ, Q);
  not not_3 (nE, E);
  not not_4 (IRQ_t, IRQ);
  // Probe on {DataIn[7:4], multiplexer_1_out}
  Multiplexer #(.width(4), .disabled(0), .enable("false")) multiplexer_1 (
    .in0(DataIn[3:0]), .in1({3'b111, not_1_out[0]}), .out(multiplexer_1_out), .sel(JUMP_OP));
  and U13A (U13A_out, S0, Bit1_qn);
  or U15B (U15B_out, U13A_out, U14A_out);
  not not_5 (not_5_out, U14A_out);
  not not_6 (not_6_out, nReset);
  and U14A (U14A_out, FlagIn[5], IQRH, S0, S1);
  D_Flip_Flop INTH (.clk(E), .D(IRQ_t), .Q(IQRH), .reset(U13B_out));  // open: Qn, preset, en
  and U13B (U13B_out, S1, Bit0_qn);
  Multiplexer #(.width(8), .disabled(0), .enable("false")) multiplexer_2 (
    .in0({DataIn[7:4], multiplexer_1_out}), .in1({6'b111000, S1, S0}), .out(multiplexer_2_out), .sel(U15C_out));
  or U15C (U15C_out, Bit1_qn, Bit0_qn);
  D_Flip_Flop Bit1 (.clk(StateClock), .D(U15B_out), .Q(S1), .Qn(Bit1_qn), .reset(not_6_out));  // open: preset, en
  D_Flip_Flop Bit0 (.clk(StateClock), .D(not_5_out), .Q(S0), .Qn(Bit0_qn), .reset(not_6_out));  // open: preset, en
  D_Flip_Flop StepControl (.clk(Q), .D(StepUpdate), .Q(StepCtrl), .preset(not_7_out));  // open: Qn, en, reset
  not not_7 (not_7_out, nReset);
  // Probe on multiplexer_2_out
  or U24C (\Set_μROM_Address , E, U21A_out);
  D_Flip_Flop Stage_Control (.clk(nE), .D(StepUpdate), .Qn(StateClock), .reset(not_8_out));  // open: Q, preset, en
  not not_8 (not_8_out, U21A_out);
  // Probe on STEP
  uROM_B urom_b_1 (
    .Load(\Set_μROM_Address ), .Update(nQ), .STEP_MON(STEP), .CtrlSignal({StepUpdate, urom_b_1_ctrlsignal}));  // open: OpeCode
  and U21A (U21A_out, nReset, nQ);
  xor U11A (JL, FlagIn[3], FlagIn[7]);
  // Probe on {StepUpdate, urom_b_1_ctrlsignal}
  not U12C (U12C_out, DataIn[4]);
  nor nor_1 (JG, JL, FlagIn[6]);
  and U14B (U14B_out, U12C_out, DataIn[5], DataIn[6], DataIn[7]);
  and and_1 (and_1_out[12], urom_b_1_ctrlsignal[12], ~urom_b_1_ctrlsignal[23]);  // AND_Gate
  or or_1 (and_1_out[17], urom_b_1_ctrlsignal[17], urom_b_1_ctrlsignal[23]);
  not not_9 (not_9_out, DataIn[0]);
  Multiplexer #(.select(2), .enable("false")) multiplexer_3 (
    .in0(FlagIn[0]), .in1(FlagIn[3]), .in2(FlagIn[6]), .in3(FlagIn[7]), .out(multiplexer_3_out),
    .sel(DataIn[2:1]));
  Register #(.width(32)) Ctrl_Signal (
    .D({StepUpdate, urom_b_1_ctrlsignal[30:18], and_1_out[17], urom_b_1_ctrlsignal[16:13], and_1_out[12], urom_b_1_ctrlsignal[11:0]}),
    .Q({Ctrl_Signal_q[31], ExBusControl, EX, RegisterControl}), .clk(nE), .clr(not_10_out));  // open: en
  not not_10 (not_10_out, nReset);
  assign DataOut = not_12_out ? HCT574_q : 8'bz;  // Controlled_Buffer controlled_buffer_1
  Register HCT574 (.D(DataIn), .Q(HCT574_q), .clk(nE));  // open: en, clr
  not not_11 (not_11_out, DataIn[3]);
  xor U11B (U11B_out, not_9_out, multiplexer_3_out);
  // Probe on RegisterControl
  not not_12 (not_12_out, urom_b_1_ctrlsignal[23]);
  and U20A (U20A_out, ~DataIn[1], ~DataIn[2], DataIn[3]);  // AND_Gate
  not not_13 (not_13_out, DataIn[0]);
  and and_2 (and_2_out, not_11_out, U11B_out);
  assign DataOut = urom_b_1_ctrlsignal[23] ? urom_b_1_ctrlsignal[17:10] : 8'bz;  // Controlled_Buffer controlled_buffer_2
  or or_2 (or_2_out, U20A_out, not_11_out);
  and and_3 (and_3_out, JL, U20A_out, not_13_out);
  and and_4 (and_4_out, JG, U20A_out, DataIn[0]);
  or or_3 (or_3_out, and_3_out, and_4_out);
  and and_5 (JUMP_OP, or_2_out, U14B_out);
  or or_4 (nDO_JUMP, or_3_out, and_2_out);

  // Other names for the same wires on the sheet: CLK = E; DO_JUMP = nDO_JUMP; CY = FlagIn[0]; OV = FlagIn[3];
  //   SingleStep = FlagIn[4]; INT_EN = FlagIn[5]; ZF = FlagIn[6]; SF = FlagIn[7]

  // Notes on the sheet:
  //   nReset: pull=up
  //   U10A
  //   U18
  //   U22,U23
  //   U17A
  //   U17B
  //   キャリー時にμ命令スキップを追加（C7)
  //   μROM_IDX
  //   U25B
  //   U25A
  //   IRQ Holhちう
  //   0:JL / 1:JG
  //   E-Line
  //   10-17
  //   23
  //   U16
  //   U29
  //   U20D,F
  //   U28
endmodule

module Executer (
  input  Q,
  input  E,
  input  Reset,
  input  [11:0] STEP,
  input  [7:0] DataIn,
  input  [23:0] RegisterCtrl,
  output [7:0] FlagRegisterOut,
  output TraceFlag,
  output [7:0] DataOut,
  output [15:0] AddrOut
);

  wire alu8c_1_cy, and_1_out, carryselector_1_cc, decoder_1_out0, decoder_1_out1, decoder_1_out2,
       decoder_1_out3, decoder_1_out4, decoder_1_out5, decoder_1_out6, decoder_1_out7, decoder_2_out0,
       decoder_2_out1, decoder_2_out2, decoder_2_out3, nE, not_3_out, nQ, shiter_1_cout;
  wire [6:0] multiplexer_3_out;
  wire [7:0] alu8c_1_alu_out, Buff1_ALU_A_q, Buff2_ALU_B_q, controlled_buffer_1_out, multiplexer_1_out,
       multiplexer_5_out, R0_q, R1_q, R2_q, R3_q, shiter_1_y;
  wire [15:0] A0_q, A1_q, CP_q, multiplexer_2_out, SP_q;

  not not_1 (nQ, Q);
  not not_2 (nE, E);
  // Probe on STEP
  // Probe on DataIn
  Decoder #(.select(3), .disabled(0)) decoder_1 (
    .out0(decoder_1_out0), .out1(decoder_1_out1), .out2(decoder_1_out2), .out3(decoder_1_out3),
    .out4(decoder_1_out4), .out5(decoder_1_out5), .out6(decoder_1_out6), .out7(decoder_1_out7),
    .sel(RegisterCtrl[16:14]), .en(and_1_out));
  and and_1 (and_1_out, RegisterCtrl[13], ~nE, ~Q);  // AND_Gate
  Register R0 (.D(DataOut), .en(1'b1), .Q(R0_q), .clk(decoder_1_out0));  // open: clr
  Register R1 (.D(DataOut), .en(1'b1), .Q(R1_q), .clk(decoder_1_out1));  // open: clr
  Register R2 (.D(DataOut), .en(1'b1), .Q(R2_q), .clk(decoder_1_out2));  // open: clr
  Register R3 (.D(DataOut), .en(1'b1), .Q(R3_q), .clk(decoder_1_out3));  // open: clr
  Register #(.width(16)) A0 (.D(AddrOut), .en(1'b1), .Q(A0_q), .clk(decoder_1_out4));  // open: clr
  Register #(.width(16)) A1 (.D(AddrOut), .en(1'b1), .Q(A1_q), .clk(decoder_1_out5));  // open: clr
  Register #(.width(16)) CP (.D(AddrOut), .en(1'b1), .Q(CP_q), .clk(decoder_1_out6));  // open: clr
  Register #(.width(16)) SP (.D(AddrOut), .en(1'b1), .Q(SP_q), .clk(decoder_1_out7));  // open: clr
  Multiplexer #(.select(2), .width(8), .disabled(0), .enable("false")) multiplexer_1 (
    .in0(R0_q), .in1(R1_q), .in2(R2_q), .in3(R3_q), .out(multiplexer_1_out), .sel(RegisterCtrl[9:8]));
  not not_3 (not_3_out, RegisterCtrl[10]);
  Decoder #(.select(2), .disabled(0)) decoder_2 (
    .out0(decoder_2_out0), .out1(decoder_2_out1), .out2(decoder_2_out2), .out3(decoder_2_out3),
    .sel(RegisterCtrl[9:8]), .en(RegisterCtrl[10]));
  // Probe on controlled_buffer_1_out
  assign controlled_buffer_1_out = not_3_out ? multiplexer_1_out : 8'bz;  // Controlled_Buffer controlled_buffer_1
  assign controlled_buffer_1_out = decoder_2_out2 ? DataIn : 8'bz;  // Controlled_Buffer U56
  assign controlled_buffer_1_out = decoder_2_out3 ? DataOut : 8'bz;  // Controlled_Buffer U64
  Multiplexer #(.select(2), .width(16), .disabled(0), .enable("false")) multiplexer_2 (
    .in0(A0_q), .in1(A1_q), .in2(CP_q), .in3(SP_q), .out(multiplexer_2_out), .sel(RegisterCtrl[12:11]));
  assign controlled_buffer_1_out = decoder_2_out0 ? multiplexer_2_out[7:0] : 8'bz;  // Controlled_Buffer controlled_buffer_2
  assign controlled_buffer_1_out = decoder_2_out1 ? multiplexer_2_out[15:8] : 8'bz;  // Controlled_Buffer controlled_buffer_3
  // Probe on AddrOut
  CarrySelector carryselector_1 (
    .CY(FlagRegisterOut[0]), .CC(carryselector_1_cc), .OP0(RegisterCtrl[0]), .OP1(RegisterCtrl[1]));
  Register Buff1_ALU_A (.D(controlled_buffer_1_out), .en(RegisterCtrl[19]), .Q(Buff1_ALU_A_q), .clk(Q));  // open: clr
  Register Buff2_ALU_B (.D(controlled_buffer_1_out), .en(RegisterCtrl[20]), .Q(Buff2_ALU_B_q), .clk(Q));  // open: clr
  ALU8C alu8c_1 (
    .S(RegisterCtrl[5:2]), .CIn(carryselector_1_cc), .M(RegisterCtrl[6]), .B(Buff2_ALU_B_q),
    .A(Buff1_ALU_A_q), .CY(alu8c_1_cy), .ALU_OUT(alu8c_1_alu_out), .OV(multiplexer_3_out[3]));
  Shiter shiter_1 (
    .A(controlled_buffer_1_out), .Y(shiter_1_y), .OP(RegisterCtrl[7:0]), .CIn(carryselector_1_cc),
    .COut(shiter_1_cout), .ZIn(FlagRegisterOut[6]));
  // Probe on DataOut
  ACU acu_1 (.A({Buff2_ALU_B_q, Buff1_ALU_A_q}), .B(multiplexer_2_out), .Y(AddrOut), .OP(RegisterCtrl[5:2]));
  ZeroFlag zeroflag_1 (.A(DataOut), .Y(multiplexer_3_out[6]));
  Multiplexer #(.disabled(0), .enable("false")) multiplexer_3 (
    .in0(shiter_1_cout), .in1(alu8c_1_cy), .out(multiplexer_3_out[0]), .sel(RegisterCtrl[23]));
  Multiplexer #(.select(2), .width(8), .disabled(0), .enable("false")) multiplexer_4 (
    .in0(controlled_buffer_1_out), .in1(alu8c_1_alu_out), .in2(shiter_1_y), .in3(FlagRegisterOut),
    .out(DataOut), .sel(RegisterCtrl[23:22]));
  Multiplexer #(.width(8), .enable("false")) multiplexer_5 (
    .in0({DataOut[7], multiplexer_3_out[6], FlagRegisterOut[4], DataOut[4], multiplexer_3_out[3], 2'b01, multiplexer_3_out[0]}),
    .in1(DataOut), .out(multiplexer_5_out), .sel(RegisterCtrl[17]));
  // Probe on multiplexer_5_out
  Register Flag (.D(multiplexer_5_out), .en(RegisterCtrl[18]), .Q(FlagRegisterOut), .clk(nQ));  // open: clr
  // Probe on RegisterCtrl

  assign TraceFlag = FlagRegisterOut[4];

  // Other names for the same wires on the sheet: BuffSel[1:0] = RegisterCtrl[20:19]; CarryFlag = FlagRegisterOut[0];
  //   ZeroFlag = FlagRegisterOut[6]; ALUOP[7:0] = RegisterCtrl[7:0]; BRSel[2:0] = RegisterCtrl[10:8];
  //   WRSel[1:0] = RegisterCtrl[12:11]; RegWEn = RegisterCtrl[13]; WriteBackSel[2:0] = RegisterCtrl[16:14];
  //   STFR = RegisterCtrl[17]; FLatcEn = RegisterCtrl[18]; MISC[1:0] = RegisterCtrl[23:22]

  // Notes on the sheet:
  //   First->
  //   Writeback
  //   Selector
  //   238
  //   C7: Shifterを独立させてALU_OPの機能を拡張する
  //   139
  //   4078
  //   157
endmodule

module uROM_B (
  input  [7:0] OpeCode,
  input  Load,
  input  Update,
  output [11:0] STEP_MON,
  output [31:0] CtrlSignal
);

  wire not_1_out;

  not not_1 (not_1_out, Load);
  Counter #(.width(4), .max('hf)) _161 (
    .load(Load), .D(4'b0000), .count(not_1_out), .Q(STEP_MON[3:0]), .clk(Update));  // open: carry, clr
  Register _377 (.D(OpeCode), .en(Load), .Q(STEP_MON[11:4]), .clk(Update));  // open: clr
  ROM #(.addrWidth(12), .dataWidth(32)) rom_1 (.addr(STEP_MON), .data(CtrlSignal));  // open: sel

  // Notes on the sheet:
  //   contents of rom_1 (hex, n*v repeats v):
  //   2402000c 80121300 14*0 2402000c 80123300 14*0 2402000c 80125300 14*0 2402000c 80127300 14*0 2402040c
  //   80121300 14*0 2402040c 80123300 14*0 2402040c 80125300 14*0 2402040c 80127300 14*0 3802000c 80020000
  //   14*0 3802008c 80020000 14*0 3802010c 80020000 14*0 3802018c 80020000 14*0 3802040c 80020000 14*0
  //   3802048c 80020000 14*0 3802050c 80020000 14*0 3802058c 80020000 14*0 2402080c 6db1c 24020304
  //   80121300 12*0 2402080c 6db1c 24020304 80123300 12*0 2402080c 6db1c 24020304 80125300 12*0 2402080c
  //   6db1c 24020304 80127300 12*0 2402080c 6db1c 24020704 80121300 12*0 2402080c 6db1c 24020704 80123300
  //   12*0 2402080c 6db1c 24020704 80125300 12*0 2402080c 6db1c 24020704 80127300 12*0 2402080c 6db1c
  //   38020004 80020000 12*0 2402080c 6db1c 38020084 80020000 12*0 2402080c 6db1c 38020104 80020000 12*0
  //   2402080c 6db1c 38020184 80020000 12*0 2402080c 6db1c 38020404 80020000 12*0 2402080c 6db1c 38020484
  //   80020000 12*0 2402080c 6db1c 38020504 80020000 12*0 2402080c 6db1c 38020584 80020000 12*0 2402080c
  //   6db1c 24020c04 80121300 12*0 2402080c 6db1c 24020c04 80123300 12*0 2402080c 6db1c 24020c04 80125300
  //   12*0 2402080c 6db1c 24020c04 80127300 12*0 2402040c 121300 2402041c 80123300 12*0 2402040c 125300
  //   2402041c 80127300 12*0 2402040c 121300 2402041c 80123300 12*0 2402040c 125300 2402041c 80127300 12*0
  //   2402080c 6db1c 38020c04 80020000 12*0 2402080c 6db1c 38020c84 80020000 12*0 2402080c 6db1c 38020d04
  //   80020000 12*0 2402080c 6db1c 38020d84 80020000 12*0 3802040c 20000 3802049c 80020000 12*0 3802050c
  //   20000 3802059c 80020000 12*0 3802040c 20000 3802049c 80020000 12*0 3802050c 20000 3802059c 80020000
  //   12*0 80020000 15*0 80020000 15*0 80020000 15*0 80020000 15*0 80020000 15*0 80020000 15*0 80020000
  //   15*0 80020000 15*0 80020000 15*0 80020000 15*0 80020000 15*0 80020000 15*0 80020000 15*0 80020000
  //   15*0 80020000 15*0 80020000 15*0 80021100 15*0 80021180 15*0 80023100 15*0 80023180 15*0 80025000
  //   15*0 80025080 15*0 80027000 15*0 80027080 15*0 80021080 15*0 80023000 15*0 80025180 15*0 80027100
  //   15*0 8002d00c 15*0 8002f00c 15*0 8002d40c 15*0 8002f40c 15*0 21200 80023280 14*0 21600 80023680 14*0
  //   23200 80025280 14*0 23600 80025680 14*0 60000 a0080 80029020 13*0 60000 a0080 8002b020 13*0 60080
  //   a0100 80029020 13*0 60080 a0100 8002b020 13*0 21200 80023280 14*0 21600 80023680 14*0 23200 80025280
  //   14*0 23600 80025680 14*0 80029800 15*0 80029c00 15*0 8002b800 15*0 8002bc00 15*0 2002fc08 18020080
  //   20000 2002fc08 18020000 80000000 10*0 2002fc08 18020280 20000 2002fc08 18020200 80000000 10*0 60000
  //   21080 80423068 13*0 60100 25180 80427068 13*0 2002fc08 18020280 2002fc08 18020200 80000000 11*0
  //   2002fc08 18020680 2002fc08 18020600 80000000 11*0 2002fc08 18020a80 2002fc08 18020a00 80000000 11*0
  //   2402080c 6db1c 8002fc04 13*0 24020f0c 121f0c 2fc1c 24020f0c 123f0c 8002fc1c 10*0 24020f0c 125f0c
  //   2fc1c 24020f0c 127f0c 8002fc1c 10*0 260015 80203015 14*0 260115 80207015 14*0 24020c0c 6ff1c
  //   24020c0c aff1c 80029020 11*0 24020c0c 6ff1c 24020c0c aff1c 8002b020 11*0 24020c0c 6ff1c 24020c0c
  //   aff1c 8002d020 11*0 24020c0c 6ff1c 24020c0c aff1c 8002f020 11*0 60000 a0080 80029000 13*0 60000
  //   a0080 8002b400 13*0 60400 a0100 80029000 13*0 60400 a0100 8002b400 13*0 60000 21100 425068 60080
  //   23180 80427068 10*0 60200 a0280 2940c 8002b020 12*0 60000 a0080 25200 27280 80029020 11*0 60100
  //   a0180 25600 27680 8002b020 11*0 2402080c 121300 8002d81c 13*0 2402080c 123300 8002d81c 13*0 2402080c
  //   125300 8002d81c 13*0 2402080c 127300 8002d81c 13*0 2402080c 6db1c 2402080c adb1c 80029020 11*0
  //   2402080c 6db1c 2402080c adb1c 8002b020 11*0 2402080c 6db1c 2402080c adb1c 8002d020 11*0 2402080c
  //   6db1c 2402080c adb1c 8002f020 11*0 60000 2a0033 80201033 13*0 60000 2a00b3 80201033 13*0 60000
  //   2a0133 80201033 13*0 60000 2a01b3 80201033 13*0 60080 2a0033 80203033 13*0 60000 2402080c adb1c
  //   80201033 12*0 60080 2a0133 80203033 13*0 60080 2a01b3 80203033 13*0 60000 2a000e 8020100e 13*0 60000
  //   2a008e 8020100e 13*0 60000 2a010e 8020100e 13*0 60000 2a018e 8020100e 13*0 60080 2a000e 8020300e
  //   13*0 60000 2402080c adb1c 8020100e 12*0 60080 2a010e 8020300e 13*0 60080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
endmodule

module uROM_C (
  input  [7:0] OpeCode,
  input  Load,
  input  Update,
  output [11:0] STEP_MON,
  output [31:0] CtrlSignal
);

  wire not_1_out;
  wire [9:0] rom_1_data;

  ROM #(.dataWidth(10)) rom_1 (.addr(OpeCode), .data(rom_1_data));  // open: sel
  not not_1 (not_1_out, Load);
  Counter #(.width(10), .max('h3ff)) counter_1 (
    .load(Load), .D(rom_1_data), .count(not_1_out), .Q(STEP_MON[9:0]), .clk(Update));  // open: carry, clr
  ROM #(.addrWidth(10), .dataWidth(32)) rom_2 (.addr(STEP_MON[9:0]), .data(CtrlSignal));  // open: sel

  assign STEP_MON[11:10] = 2'b00;

  // Notes on the sheet:
  //   2段にしてROM小さくした
  //   μOPEROM
  //   contents of rom_1 (hex, n*v repeats v):
  //   0 2 4 6 8 a c e 10 12 14 16 18 1a 1c 1e 20 24 28 2c 30 34 38 3c 40 44 48 4c 50 54 58 5c 60 64 68 6c
  //   70 74 78 7c 80 84 88 8c 90 94 98 9c a0 a1 a2 a3 a4 a5 a6 a7 a8 a9 aa ab ac ad ae af b0 b1 b2 b3 b4
  //   b5 b6 b7 b8 b9 ba bb bc bd be bf c0 c2 c4 c6 c8 cb ce d1 d4 d6 d8 da dc dd de df e0 e6 ec ed ee f4
  //   fa 100 101 105 109 10b 10d 112 117 11c 121 124 127 12a 12d 133 137 13c 141 144 147 14a 14d 152 157
  //   15c 161 164 167 16a 16d 170 174 177 17a 17d 180 183 186 189 18d 190 193 196 199 19c 19f 1a2 1a6 1a9
  //   1ac 1af 1b2 1b5 1b8 1bb 1bf 1c2 1c5 1c8 1cb 1ce 1d1 1d4 1d8 1db 1de 1e1 1e4 1e7 1ea 1ed 1f1 1f4 1f7
  //   1fa 1fd 200 203 206 20a 20d 210 213 216 219 21c 21f 223 226 229 22b 22d 22f 231 233 235 237 239 23b
  //   23d 23f 241 243 245 247 249 24a 24b 24c 24d 24f 251 252 253 254 255 256 257 259 25b 25c 25d 25f 261
  //   270 271 272 273 274 275 276 277 278 279 287 295 298 299 29a 29b 29c 29d 2a0 2a3 2a6 2a9 2af 2b5 2bf
  //   2c0 2c1 2ca 2cf
  //   contents of rom_2 (hex, n*v repeats v):
  //   2402000c 80121300 2402000c 80123300 2402000c 80125300 2402000c 80127300 2402040c 80121300 2402040c
  //   80123300 2402040c 80125300 2402040c 80127300 3802000c 80020000 3802008c 80020000 3802010c 80020000
  //   3802018c 80020000 3802040c 80020000 3802048c 80020000 3802050c 80020000 3802058c 80020000 2402080c
  //   6db1c 24020304 80121300 2402080c 6db1c 24020304 80123300 2402080c 6db1c 24020304 80125300 2402080c
  //   6db1c 24020304 80127300 2402080c 6db1c 24020704 80121300 2402080c 6db1c 24020704 80123300 2402080c
  //   6db1c 24020704 80125300 2402080c 6db1c 24020704 80127300 2402080c 6db1c 38020004 80020000 2402080c
  //   6db1c 38020084 80020000 2402080c 6db1c 38020104 80020000 2402080c 6db1c 38020184 80020000 2402080c
  //   6db1c 38020404 80020000 2402080c 6db1c 38020484 80020000 2402080c 6db1c 38020504 80020000 2402080c
  //   6db1c 38020584 80020000 2402080c 6db1c 24020c04 80121300 2402080c 6db1c 24020c04 80123300 2402080c
  //   6db1c 24020c04 80125300 2402080c 6db1c 24020c04 80127300 2402040c 121300 2402041c 80123300 2402040c
  //   125300 2402041c 80127300 2402040c 121300 2402041c 80123300 2402040c 125300 2402041c 80127300
  //   2402080c 6db1c 38020c04 80020000 2402080c 6db1c 38020c84 80020000 2402080c 6db1c 38020d04 80020000
  //   2402080c 6db1c 38020d84 80020000 3802040c 20000 3802049c 80020000 3802050c 20000 3802059c 80020000
  //   3802040c 20000 3802049c 80020000 3802050c 20000 3802059c 17*80020000 80021100 80021180 80023100
  //   80023180 80025000 80025080 80027000 80027080 80021080 80023000 80025180 80027180 8002d00c 8002f00c
  //   8002d40c 8002f40c 21200 80023280 21600 80023680 23200 80025280 23600 80025680 60000 a0080 80029020
  //   60000 a0080 8002b020 60080 a0100 80029020 60080 a0100 8002b020 21200 80023280 21600 80023680 23200
  //   80025280 23600 80025680 80029800 80029c00 8002b800 8002bc00 2002fc08 18020000 20000 2002fc08
  //   18020080 80000000 2002fc08 18020200 20000 2002fc08 18020280 80000000 0 0 2002fc08 18020280 20000
  //   2002fc08 18020200 80000000 2002fc08 18020680 20000 2002fc08 18020600 80000000 2002fc08 18020a80
  //   20000 2002fc08 18020a00 80000000 0 24021f0c 2fc1c 24023f0c 8002fc1c 24025f0c 2fc1c 24027f0c 8002fc1c
  //   260015 80203015 260115 80207015 24020c0c 6ff1c 24020c0c aff1c 80029020 24020c0c 6ff1c 24020c0c aff1c
  //   8002b020 24020c0c 6ff1c 24020c0c aff1c 8002d020 24020c0c 6ff1c 24020c0c aff1c 8002f020 60000 a0080
  //   80029000 60000 a0080 8002b400 60400 a0100 80029000 60400 a0100 8002b400 60000 21100 425068 60080
  //   23180 80427068 60200 a0280 2940c 8002b020 60000 a0080 25200 27280 80029020 60100 a0180 25600 27680
  //   8002b020 2402080c 121000 8002db1c 2402080c 123000 8002db1c 2402080c 125000 8002db1c 2402080c 127000
  //   8002db1c 2402080c 6db1c 2402080c adb1c 80029020 2402080c 6db1c 2402080c adb1c 8002b020 2402080c
  //   6db1c 2402080c adb1c 8002d020 2402080c 6db1c 2402080c adb1c 8002f020 60000 2a0033 80201033 60000
  //   2a00b3 80201033 60000 2a0133 80201033 60000 2a01b3 80201033 60080 2a0033 80203033 60080 24020800
  //   adb1c 80201033 60080 2a0133 80203033 60080 2a01b3 80203033 60000 2a000e 8020100e 60000 2a008e
  //   8020100e 60000 2a010e 8020100e 60000 2a018e 8020100e 60080 2a000e 8020300e 60080 24020800 adb1c
  //   8020100e 60080 2a010e 8020300e 60080 2a018e 8020300e 60000 2a0030 80201030 60000 2a00b0 80201030
  //   60000 2a0130 80201030 60000 2a01b0 80201030 60080 2a0030 80203030 60080 24020800 adb1c 80201030
  //   60080 2a0130 80203030 60080 2a01b0 80203030 60000 2a000c 8020100c 60000 2a008c 8020100c 60000 2a010c
  //   8020100c 60000 2a018c 8020100c 60080 2a000c 8020300c 60080 24020800 adb1c 8020100c 60080 2a010c
  //   8020300c 60080 2a018c 8020300c 60000 4a0060 80401060 60000 4a00e0 80401060 60000 4a0160 80401060
  //   60000 4a01e0 80401060 60080 4a0060 80403060 60080 24020800 adb1c 80401060 60080 4a0160 80403060
  //   60080 4a01e0 80403060 60000 2a000e 8020000e 60000 2a008e 8020000e 60000 2a010e 8020000e 60000 2a018e
  //   8020000e 60080 2a000e 8020000e 60080 24020800 adb1c 8020000e 60080 2a010e 8020000e 60080 2a018e
  //   8020000e 60000 4a0058 80401058 60000 4a00d8 80401058 60000 4a0158 80401058 60000 4a01d8 80401058
  //   60080 4a0058 80403058 60080 24020800 adb1c 80401058 60080 4a0158 80403058 60080 4a01d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
endmodule

module uROM_D (
  input  [7:0] OpeCode,
  input  Load,
  input  Update,
  input  DOutClk,
  output [11:0] STEP_MON,
  output [31:0] CtrlSignal
);

  wire not_1_out;
  wire [9:0] register_1_q, rom_1_data;

  ROM #(.dataWidth(10)) rom_1 (.addr(OpeCode), .data(rom_1_data));  // open: sel
  not not_1 (not_1_out, Load);
  Register #(.width(10)) register_1 (.D(STEP_MON[9:0]), .Q(register_1_q), .clk(DOutClk));  // open: en, clr
  Counter #(.width(10), .max('h3ff)) counter_1 (
    .load(Load), .D(rom_1_data), .count(not_1_out), .Q(STEP_MON[9:0]), .clk(Update));  // open: carry, clr
  ROM #(.addrWidth(10), .dataWidth(32)) rom_2 (.addr(register_1_q), .data(CtrlSignal));  // open: sel

  assign STEP_MON[11:10] = 2'b00;

  // Notes on the sheet:
  //   2段にしてROM小さくした
  //   μOPEROM
  //   contents of rom_1 (hex, n*v repeats v):
  //   0 2 4 6 8 a c e 10 12 14 16 18 1a 1c 1e 20 24 28 2c 30 34 38 3c 40 44 48 4c 50 54 58 5c 60 64 68 6c
  //   70 74 78 7c 80 84 88 8c 90 94 98 9c a0 a1 a2 a3 a4 a5 a6 a7 a8 a9 aa ab ac ad ae af b0 b1 b2 b3 b4
  //   b5 b6 b7 b8 b9 ba bb bc bd be bf c0 c2 c4 c6 c8 cb ce d1 d4 d6 d8 da dc dd de df e0 e6 ec ef f2 f7
  //   fc 101 104 10a 110 112 114 119 11e 123 128 12b 12e 131 134 13a 13e 143 148 14b 14e 151 154 159 15e
  //   163 168 16b 16e 171 174 177 17b 17e 181 184 187 18a 18d 190 194 197 19a 19d 1a0 1a3 1a6 1a9 1ad 1b0
  //   1b3 1b6 1b9 1bc 1bf 1c2 1c6 1c9 1cc 1cf 1d2 1d5 1d8 1db 1df 1e2 1e5 1e8 1eb 1ee 1f1 1f4 1f8 1fb 1fe
  //   201 204 207 20a 20d 211 214 217 21a 21d 220 223 226 22a 22d 230 232 234 236 238 23a 23c 23e 240 242
  //   244 246 248 24a 24c 24e 250 251 252 253 254 256 258 25a 25c 25d 25e 25f 260 262 264 265 266 268 26a
  //   278 279 27a 27b 27c 27d 27e 27f 280 281 28b 297 29a 29b 29c 29d 29e 29f 2a2 2a5 2a8 2ab 2b1 2b7 2c0
  //   2c1 2c5 2ce 2d3
  //   contents of rom_2 (hex, n*v repeats v):
  //   2402000c 80121300 2402000c 80123300 2402000c 80125300 2402000c 80127300 2402040c 80121300 2402040c
  //   80123300 2402040c 80125300 2402040c 80127300 3802000c 80020000 3802008c 80020000 3802010c 80020000
  //   3802018c 80020000 3802040c 80020000 3802048c 80020000 3802050c 80020000 3802058c 80020000 2402080c
  //   6db1c 24020304 80121300 2402080c 6db1c 24020304 80123300 2402080c 6db1c 24020304 80125300 2402080c
  //   6db1c 24020304 80127300 2402080c 6db1c 24020704 80121300 2402080c 6db1c 24020704 80123300 2402080c
  //   6db1c 24020704 80125300 2402080c 6db1c 24020704 80127300 2402080c 6db1c 38020004 80020000 2402080c
  //   6db1c 38020084 80020000 2402080c 6db1c 38020104 80020000 2402080c 6db1c 38020184 80020000 2402080c
  //   6db1c 38020404 80020000 2402080c 6db1c 38020484 80020000 2402080c 6db1c 38020504 80020000 2402080c
  //   6db1c 38020584 80020000 2402080c 6db1c 24020c04 80121300 2402080c 6db1c 24020c04 80123300 2402080c
  //   6db1c 24020c04 80125300 2402080c 6db1c 24020c04 80127300 2402040c 121300 2402041c 80123300 2402040c
  //   125300 2402041c 80127300 2402040c 121300 2402041c 80123300 2402040c 125300 2402041c 80127300
  //   2402080c 6db1c 38020c04 80020000 2402080c 6db1c 38020c84 80020000 2402080c 6db1c 38020d04 80020000
  //   2402080c 6db1c 38020d84 80020000 3802040c 20000 3802049c 80020000 3802050c 20000 3802059c 80020000
  //   3802040c 20000 3802049c 80020000 3802050c 20000 3802059c 17*80020000 80021100 80021180 80023100
  //   80023180 80025000 80025080 80027000 80027080 80021080 80023000 80025180 80027100 8002d00c 8002f00c
  //   8002d40c 8002f40c 21200 80023280 21600 80023680 23200 80025280 23600 80025680 60000 a0080 80029020
  //   60000 a0080 8002b020 60080 a0100 80029020 60080 a0100 8002b020 21200 80023280 21600 80023680 23200
  //   80025280 23600 80025680 80029800 80029c00 8002b800 8002bc00 2002fc08 18020080 20000 2002fc08
  //   18020000 80000000 2002fc08 18020280 20000 2002fc08 18020200 80000000 60000 21080 80423068 60100
  //   25180 80427068 2002fc08 18020280 2002fc08 18020200 80000000 2002fc08 18020680 2002fc08 18020600
  //   80000000 2002fc08 18020a80 2002fc08 18020a00 80000000 2402080c 6db1c 8002fc04 24020f0c 121f0c 2fc1c
  //   24020f0c 123f0c 8002fc1c 24020f0c 125f0c 2fc1c 24020f0c 127f0c 8002fc1c 260015 80203015 260115
  //   80207015 24020c0c 6ff1c 24020c0c aff1c 80029020 24020c0c 6ff1c 24020c0c aff1c 8002b020 24020c0c
  //   6ff1c 24020c0c aff1c 8002d020 24020c0c 6ff1c 24020c0c aff1c 8002f020 60000 a0080 80029000 60000
  //   a0080 8002b400 60400 a0100 80029000 60400 a0100 8002b400 60000 21100 425068 60080 23180 80427068
  //   60200 a0280 2940c 8002b020 60000 a0080 25200 27280 80029020 60100 a0180 25600 27680 8002b020
  //   2402080c 121300 8002d81c 2402080c 123300 8002d81c 2402080c 125300 8002d81c 2402080c 127300 8002d81c
  //   2402080c 6db1c 2402080c adb1c 80029020 2402080c 6db1c 2402080c adb1c 8002b020 2402080c 6db1c
  //   2402080c adb1c 8002d020 2402080c 6db1c 2402080c adb1c 8002f020 60000 2a0033 80201033 60000 2a00b3
  //   80201033 60000 2a0133 80201033 60000 2a01b3 80201033 60080 2a0033 80203033 60000 2402080c adb1c
  //   80201033 60080 2a0133 80203033 60080 2a01b3 80203033 60000 2a000e 8020100e 60000 2a008e 8020100e
  //   60000 2a010e 8020100e 60000 2a018e 8020100e 60080 2a000e 8020300e 60000 2402080c adb1c 8020100e
  //   60080 2a010e 8020300e 60080 2a018e 8020300e 60000 2a0030 80201030 60000 2a00b0 80201030 60000 2a0130
  //   80201030 60000 2a01b0 80201030 60080 2a0030 80203030 60000 2402080c adb1c 80201030 60080 2a0130
  //   80203030 60080 2a01b0 80203030 60000 2a000c 8020100c 60000 2a008c 8020100c 60000 2a010c 8020100c
  //   60000 2a018c 8020100c 60080 2a000c 8020300c 60000 2402080c adb1c 8020100c 60080 2a010c 8020300c
  //   60080 2a018c 8020300c 60000 4a0060 80401060 60000 4a00e0 80401060 60000 4a0160 80401060 60000 4a01e0
  //   80401060 60080 4a0060 80403060 60000 2402080c adb1c 80401060 60080 4a0160 80403060 60080 4a01e0
  //   80403060 60000 2a000e 8020000e 60000 2a008e 8020000e 60000 2a010e 8020000e 60000 2a018e 8020000e
  //   60080 2a000e 8020000e 60000 2402080c adb1c 8020000e 60080 2a010e 8020000e 60080 2a018e 8020000e
  //   60000 4a0058 80401058 60000 4a00d8 80401058 60000 4a0158 80401058 60000 4a01d8 80401058 60080 4a0058
  //   80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
endmodule

module uROM_C7 (
  input  [7:0] in_1,
  input  Load,
  input  Update,
  input  DOutClk,
  output [11:0] STEP_MON,
  output [31:0] CtrlSignal
);

  wire not_1_out;
  wire [9:0] register_1_q, rom_1_data;

  ROM #(.dataWidth(10)) rom_1 (.addr(in_1), .data(rom_1_data));  // open: sel
  not not_1 (not_1_out, Load);
  Register #(.width(10)) register_1 (.D(STEP_MON[9:0]), .Q(register_1_q), .clk(DOutClk));  // open: en, clr
  Counter #(.width(10), .max('h3ff)) counter_1 (
    .load(Load), .D(rom_1_data), .count(not_1_out), .Q(STEP_MON[9:0]), .clk(Update));  // open: carry, clr
  ROM #(.addrWidth(10), .dataWidth(32)) rom_2 (.addr(register_1_q), .data(CtrlSignal));  // open: sel

  assign STEP_MON[11:10] = 2'b00;

  // Notes on the sheet:
  //   contents of rom_1 (hex, n*v repeats v):
  //   0 2 4 6 8 a c e 10 12 14 16 18 1a 1c 1e 20 24 28 2c 30 34 38 3c 40 44 48 4c 50 54 58 5c 60 64 68 6c
  //   70 74 78 7c 80 84 88 8c 90 94 98 9c a0 a1 a2 a3 a4 a5 a6 a7 a8 a9 aa ab ac ad ae af b0 b1 b2 b3 b4
  //   b5 b6 b7 b8 b9 ba bb bc bd be bf c0 c2 c4 c6 c8 cb ce d1 d4 d6 d8 da dc dd de df e0 e6 ec ef f2 f7
  //   fc 101 104 10a 110 112 114 119 11e 123 128 12b 12e 131 134 13a 13e 143 148 14b 14e 151 154 159 15e
  //   163 168 16b 16e 171 174 177 17b 17e 181 184 187 18a 18d 190 194 197 19a 19d 1a0 1a3 1a6 1a9 1ad 1b0
  //   1b3 1b6 1b9 1bc 1bf 1c2 1c6 1c9 1cc 1cf 1d2 1d5 1d8 1db 1df 1e2 1e5 1e8 1eb 1ee 1f1 1f4 1f8 1fb 1fe
  //   201 204 207 20a 20d 211 214 217 21a 21d 220 223 226 22a 22d 230 232 234 236 238 23a 23c 23e 240 242
  //   244 246 248 24a 24c 24e 250 251 252 253 254 256 258 25a 25c 25d 25e 25f 260 262 264 265 266 268 26a
  //   278 279 27a 27b 27c 27d 27e 27f 280 281 28b 297 29a 29b 29c 29d 29e 29f 2a2 2a5 2a8 2ab 2b1 2b7 2c0
  //   2c1 2c5 2ce 2d3
  //   μOPEROM
  //   contents of rom_2 (hex, n*v repeats v):
  //   2402000c 80121300 2402000c 80123300 2402000c 80125300 2402000c 80127300 2402040c 80121300 2402040c
  //   80123300 2402040c 80125300 2402040c 80127300 3802000c 80020000 3802008c 80020000 3802010c 80020000
  //   3802018c 80020000 3802040c 80020000 3802048c 80020000 3802050c 80020000 3802058c 80020000 2402080c
  //   6db1c 24020304 80121300 2402080c 6db1c 24020304 80123300 2402080c 6db1c 24020304 80125300 2402080c
  //   6db1c 24020304 80127300 2402080c 6db1c 24020704 80121300 2402080c 6db1c 24020704 80123300 2402080c
  //   6db1c 24020704 80125300 2402080c 6db1c 24020704 80127300 2402080c 6db1c 38020004 80020000 2402080c
  //   6db1c 38020084 80020000 2402080c 6db1c 38020104 80020000 2402080c 6db1c 38020184 80020000 2402080c
  //   6db1c 38020404 80020000 2402080c 6db1c 38020484 80020000 2402080c 6db1c 38020504 80020000 2402080c
  //   6db1c 38020584 80020000 2402080c 6db1c 24020c04 80121300 2402080c 6db1c 24020c04 80123300 2402080c
  //   6db1c 24020c04 80125300 2402080c 6db1c 24020c04 80127300 2402040c 121300 2402041c 80123300 2402040c
  //   125300 2402041c 80127300 2402040c 121300 2402041c 80123300 2402040c 125300 2402041c 80127300
  //   2402080c 6db1c 38020c04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
endmodule

module ACU (
  input  [15:0] A,
  input  [15:0] B,
  input  [3:0] OP,
  output [15:0] Y
);

  wire nand_1_out, not_1_out, or_1_out, or_2_out;
  wire [7:0] addrexmux_1_y, addrexmux_2_y;
  wire [15:0] multiplexer_1_out;

  Multiplexer #(.width(16), .disabled(0), .enable("false")) multiplexer_1 (
    .in0(B), .in1({16{1'b0}}), .out(multiplexer_1_out), .sel(OP[3]));
  not not_1 (not_1_out, A[7]);
  nand nand_1 (nand_1_out, OP[0], or_1_out);
  or or_1 (or_1_out, OP[1], not_1_out);
  or or_2 (or_2_out, OP[1], OP[0]);
  AddrExMux addrexmux_1 (.A(A[7:0]), .Sel(OP[1]), .B(nand_1_out), .Y(addrexmux_1_y));
  AddrExMux addrexmux_2 (.A(A[15:8]), .Sel(or_2_out), .B(nand_1_out), .Y(addrexmux_2_y));
  // Probe on addrexmux_1_y
  // Probe on addrexmux_2_y
  Adder #(.width(16)) adder_1 (
    .a({addrexmux_2_y, addrexmux_1_y}), .b(multiplexer_1_out), .out(Y), .cin(OP[2]));  // open: cout
endmodule

// Mux
module AddrExMux (
  input  [7:0] A,
  input  B,
  input  Sel,
  output [7:0] Y
);

  Multiplexer #(.width(8), .disabled(0), .enable("false")) multiplexer_1 (.in0(A), .in1({8{B}}), .out(Y), .sel(Sel));
endmodule

module ALU8C (
  input  M,
  input  [7:0] A,
  input  [7:0] B,
  input  [3:0] S,
  input  CIn,
  output CY,
  output OV,
  output [7:0] ALU_OUT
);

  wire alu8a_1_cy, xor_2_out, xor_3_out, xor_4_out;
  wire [7:0] alu8a_1_y, alu8l_1_y;

  ALU8L alu8l_1 (.A(A), .B(B), .S(S), .Y(alu8l_1_y));
  ALU8A alu8a_1 (.B(alu8l_1_y), .A(A), .Cin(CIn), .CY(alu8a_1_cy), .Y(alu8a_1_y));
  xor xor_1 (CY, M, alu8a_1_cy);
  xor xor_2 (xor_2_out, A[7], B[7]);
  xor xor_3 (xor_3_out, A[7], alu8a_1_y[7]);
  Multiplexer #(.width(8), .disabled(0), .enable("false")) multiplexer_1 (
    .in0(alu8a_1_y), .in1(alu8l_1_y), .out(ALU_OUT), .sel(M));
  xor xor_4 (xor_4_out, S[3], xor_2_out);
  and and_1 (OV, xor_4_out, xor_3_out);

  // Notes on the sheet:
  //   Over flow flag.
endmodule

module ALU8L (
  input  [7:0] A,
  input  [7:0] B,
  input  [3:0] S,
  output [7:0] Y
);

  Multiplexer #(.select(2), .disabled(0), .enable("false")) multiplexer_1 (
    .in0(S[0]), .in1(S[1]), .in2(S[2]), .in3(S[3]), .out(Y[4]), .sel({B[4], A[4]}));
  Multiplexer #(.select(2), .disabled(0), .enable("false")) multiplexer_2 (
    .in0(S[0]), .in1(S[1]), .in2(S[2]), .in3(S[3]), .out(Y[5]), .sel({B[5], A[5]}));
  Multiplexer #(.select(2), .disabled(0), .enable("false")) multiplexer_3 (
    .in0(S[0]), .in1(S[1]), .in2(S[2]), .in3(S[3]), .out(Y[6]), .sel({B[6], A[6]}));
  Multiplexer #(.select(2), .disabled(0), .enable("false")) multiplexer_4 (
    .in0(S[0]), .in1(S[1]), .in2(S[2]), .in3(S[3]), .out(Y[7]), .sel({B[7], A[7]}));
  Multiplexer #(.select(2), .disabled(0), .enable("false")) multiplexer_5 (
    .in0(S[0]), .in1(S[1]), .in2(S[2]), .in3(S[3]), .out(Y[0]), .sel({B[0], A[0]}));
  Multiplexer #(.select(2), .disabled(0), .enable("false")) multiplexer_6 (
    .in0(S[0]), .in1(S[1]), .in2(S[2]), .in3(S[3]), .out(Y[1]), .sel({B[1], A[1]}));
  Multiplexer #(.select(2), .disabled(0), .enable("false")) multiplexer_7 (
    .in0(S[0]), .in1(S[1]), .in2(S[2]), .in3(S[3]), .out(Y[2]), .sel({B[2], A[2]}));
  Multiplexer #(.select(2), .disabled(0), .enable("false")) multiplexer_8 (
    .in0(S[0]), .in1(S[1]), .in2(S[2]), .in3(S[3]), .out(Y[3]), .sel({B[3], A[3]}));
endmodule

module ALU4A (
  input  [3:0] B,
  input  [3:0] A,
  input  CIn,
  output COut,
  output [3:0] Y
);

  wire and_1_out, and_2_out, and_3_out, and_4_out, and_5_out, and_6_out, and_7_out, and_8_out, and_9_out,
       and_10_out, and_11_out, and_12_out, and_13_out, and_14_out, or_2_out, or_3_out, or_4_out, xor_1_out,
       xor_2_out, xor_3_out, xor_4_out;

  xor xor_1 (xor_1_out, B[3], A[3]);
  and and_1 (and_1_out, B[3], A[3]);
  xor xor_2 (xor_2_out, B[2], A[2]);
  and and_2 (and_2_out, B[2], A[2]);
  xor xor_3 (xor_3_out, B[1], A[1]);
  and and_3 (and_3_out, B[1], A[1]);
  xor xor_4 (xor_4_out, B[0], A[0]);
  and and_4 (and_4_out, B[0], A[0]);
  and and_5 (and_5_out, xor_1_out, and_2_out);
  and and_6 (and_6_out, xor_1_out, xor_2_out, and_3_out);
  and and_7 (and_7_out, xor_1_out, xor_2_out, xor_3_out, and_4_out);
  and and_8 (and_8_out, xor_1_out, xor_2_out, xor_3_out, xor_4_out, CIn);
  and and_9 (and_9_out, xor_2_out, and_3_out);
  and and_10 (and_10_out, xor_2_out, xor_3_out, and_4_out);
  and and_11 (and_11_out, xor_2_out, xor_3_out, xor_4_out, CIn);
  and and_12 (and_12_out, xor_3_out, and_4_out);
  and and_13 (and_13_out, xor_3_out, xor_4_out, CIn);
  and and_14 (and_14_out, xor_4_out, CIn);
  or or_1 (COut, and_1_out, and_5_out, and_6_out, and_7_out, and_8_out);
  or or_2 (or_2_out, and_2_out, and_9_out, and_10_out, and_11_out);
  or or_3 (or_3_out, and_3_out, and_12_out, and_13_out);
  or or_4 (or_4_out, and_4_out, and_14_out);
  xor xor_5 (Y[3], xor_1_out, or_2_out);
  xor xor_6 (Y[2], xor_2_out, or_3_out);
  xor xor_7 (Y[1], xor_3_out, or_4_out);
  xor xor_8 (Y[0], xor_4_out, CIn);
endmodule

module ALU8A (
  input  [7:0] B,
  input  [7:0] A,
  input  Cin,
  output CY,
  output [7:0] Y
);

  wire alu4a_2_cout;

  ALU4A alu4a_1 (.B(B[7:4]), .A(A[7:4]), .CIn(alu4a_2_cout), .COut(CY), .Y(Y[7:4]));
  ALU4A alu4a_2 (.B(B[3:0]), .A(A[3:0]), .CIn(Cin), .COut(alu4a_2_cout), .Y(Y[3:0]));
endmodule

module Shiter (
  input  CIn,
  input  ZIn,
  input  [7:0] A,
  input  [7:0] OP,
  output COut,
  output [7:0] Y
);

  wire not_1_out;
  wire [0:0] multiplexer_1_out;

  not not_1 (not_1_out, ZIn);
  Multiplexer #(.select(2), .disabled(0), .enable("false")) multiplexer_1 (
    .in0(CIn), .in1(not_1_out), .in2(A[7]), .in3(1'b0), .out(multiplexer_1_out[0]), .sel(OP[1:0]));
  Multiplexer #(.select(2), .disabled(0), .enable("false")) multiplexer_2 (
    .in0(A[7]), .in1(A[0]), .in2(A[5]), .in3(multiplexer_1_out[0]), .out(COut), .sel(OP[3:2]));
  Multiplexer #(.select(2), .width(8), .disabled(0), .enable("false")) multiplexer_3 (
    .in0({A[6:0], multiplexer_1_out[0]}), .in1({multiplexer_1_out[0], A[7:1]}), .in2({A[4:0], 3'b000}),
    .in3({8{multiplexer_1_out[0]}}), .out(Y), .sel(OP[3:2]));
endmodule

module CarrySelector (
  input  CY,
  input  OP0,
  input  OP1,
  output CC
);

  wire not_1_out;

  not not_1 (not_1_out, CY);
  Multiplexer #(.select(2), .enable("false")) multiplexer_1 (
    .in0(CY), .in1(not_1_out), .in2(1'b1), .in3(1'b0), .out(CC), .sel({OP1, OP0}));
endmodule

module ZeroFlag (
  input  [7:0] A,
  output Y
);

  nor nor_1 (Y, A[0], A[1], A[2], A[3], A[4], A[5], A[6], A[7]);
endmodule

module uart_rx (
  input  serial_in,
  input  Reset,
  input  clk,
  output [7:0] dataOut,
  output DataRdy,
  output SerialCLK
);

  wire clock_1_out, d_ff_1_qn, d_ff_2_q, d_ff_2_qn, d_ff_3_qn, not_1_out, not_2_out, not_3_out, not_4_out,
       not_5_out, not_6_out, not_7_out, not_8_out, not_9_out, not_10_out, not_11_out, not_12_out, not_13_out,
       or_1_out, or_2_out;
  wire [7:0] d_ff_4_q, register_1_q;

  not not_1 (not_1_out, Reset);
  Clock clock_1 (.out(clock_1_out));
  not not_2 (not_2_out, serial_in);
  or or_1 (or_1_out, ~not_1_out, DataRdy);  // OR_Gate
  or or_2 (or_2_out, d_ff_1_qn, clock_1_out);
  D_Flip_Flop d_ff_1 (.clk(not_2_out), .D(1'b1), .Qn(d_ff_1_qn), .reset(or_1_out));  // open: Q, preset, en
  D_Flip_Flop d_ff_2 (
    .clk(or_2_out), .D(d_ff_2_qn), .Q(d_ff_2_q), .Qn(d_ff_2_qn), .reset(not_3_out));  // open: preset, en
  not not_3 (not_3_out, not_1_out);
  nor nor_1 (SerialCLK, d_ff_2_q, d_ff_3_qn);
  D_Flip_Flop d_ff_3 (.clk(d_ff_2_q), .D(d_ff_3_qn), .Qn(d_ff_3_qn), .reset(not_4_out));  // open: Q, preset, en
  not not_4 (not_4_out, not_1_out);
  D_Flip_Flop d_ff_4 (.clk(SerialCLK), .D(not_2_out), .Q(d_ff_4_q[0]), .reset(not_5_out));  // open: Qn, preset, en
  not not_5 (not_5_out, not_1_out);
  D_Flip_Flop d_ff_5 (.clk(SerialCLK), .D(d_ff_4_q[0]), .Q(d_ff_4_q[1]), .reset(not_6_out));  // open: Qn, preset, en
  not not_6 (not_6_out, not_1_out);
  D_Flip_Flop d_ff_6 (.clk(SerialCLK), .D(d_ff_4_q[1]), .Q(d_ff_4_q[2]), .reset(not_7_out));  // open: Qn, preset, en
  not not_7 (not_7_out, not_1_out);
  D_Flip_Flop d_ff_7 (.clk(SerialCLK), .D(d_ff_4_q[2]), .Q(d_ff_4_q[3]), .reset(not_8_out));  // open: Qn, preset, en
  not not_8 (not_8_out, not_1_out);
  D_Flip_Flop d_ff_8 (.clk(SerialCLK), .D(d_ff_4_q[3]), .Q(d_ff_4_q[4]), .reset(not_9_out));  // open: Qn, preset, en
  not not_9 (not_9_out, not_1_out);
  D_Flip_Flop d_ff_9 (.clk(SerialCLK), .D(d_ff_4_q[4]), .Q(d_ff_4_q[5]), .reset(not_10_out));  // open: Qn, preset, en
  not not_10 (not_10_out, not_1_out);
  D_Flip_Flop d_ff_10 (.clk(SerialCLK), .D(d_ff_4_q[5]), .Q(d_ff_4_q[6]), .reset(not_11_out));  // open: Qn, preset, en
  not not_11 (not_11_out, not_1_out);
  D_Flip_Flop d_ff_11 (.clk(SerialCLK), .D(d_ff_4_q[6]), .Q(d_ff_4_q[7]), .reset(not_12_out));  // open: Qn, preset, en
  not not_12 (not_12_out, not_1_out);
  Register register_1 (.D(d_ff_4_q), .Q(register_1_q), .clk(DataRdy));  // open: en, clr
  D_Flip_Flop d_ff_12 (.clk(SerialCLK), .D(d_ff_4_q[7]), .Q(DataRdy), .reset(not_13_out));  // open: Qn, preset, en
  not not_13 (not_13_out, not_1_out);
  assign dataOut = ~register_1_q;  // NOT_Gate not_14, 8 bits wide

  // Notes on the sheet:
  //   U1 74HC74
  //   U2 74HC74
  //   U3 74HC595
  //   U4 74HC540
  //   U5 74HC4060
  //   U6 74HC04
  //   U7 74HC32
  //   X1 19.6608MHz
  //   74HC595
  //   74HC540
endmodule

module uart_tx (
  input  [7:0] dataIn,
  input  Reset,
  input  clk,
  output out_4,
  output Done
);

  wire and_2_out, and_3_out, clock_1_out, d_ff_1_q, d_ff_1_qn, d_ff_2_q, d_ff_3_qn, d_ff_4_q, d_ff_5_q,
       d_ff_5_qn, d_ff_6_q, d_ff_7_q, d_ff_8_q, d_ff_9_q, d_ff_10_q, d_ff_11_q, d_ff_12_q, d_ff_13_q,
       d_ff_14_q, d_ff_15_q, multiplexer_1_out, multiplexer_2_out, multiplexer_3_out, multiplexer_4_out,
       multiplexer_5_out, multiplexer_6_out, multiplexer_7_out, multiplexer_8_out, not_1_out, not_2_out,
       not_3_out, not_4_out, not_5_out, not_6_out, not_7_out, not_8_out, not_9_out, not_10_out, not_11_out,
       or_1_out, xor_1_out, xor_2_out, xor_3_out;

  not not_1 (not_1_out, Reset);
  Clock clock_1 (.out(clock_1_out));
  not not_2 (not_2_out, not_1_out);
  D_Flip_Flop d_ff_1 (
    .clk(clock_1_out), .D(d_ff_1_qn), .Q(d_ff_1_q), .Qn(d_ff_1_qn), .preset(not_2_out));  // open: en, reset
  not not_3 (not_3_out, not_1_out);
  D_Flip_Flop d_ff_2 (.clk(not_5_out), .D(1'b1), .Q(d_ff_2_q), .reset(not_4_out));  // open: Qn, preset, en
  not not_4 (not_4_out, not_1_out);
  not not_5 (not_5_out, or_1_out);
  D_Flip_Flop d_ff_3 (.clk(d_ff_1_q), .D(d_ff_3_qn), .Qn(d_ff_3_qn), .preset(not_3_out));  // open: Q, en, reset
  not not_6 (not_6_out, not_1_out);
  or or_1 (or_1_out, d_ff_3_qn, Done);
  and and_1 (Done, d_ff_5_q, d_ff_8_q, ~d_ff_11_q, d_ff_13_q);  // AND_Gate
  Multiplexer #(.disabled(0), .enable("false")) multiplexer_1 (
    .in0(dataIn[0]), .in1(1'b1), .out(multiplexer_1_out), .sel(d_ff_2_q));
  D_Flip_Flop d_ff_4 (.clk(or_1_out), .D(multiplexer_1_out), .Q(d_ff_4_q));  // open: Qn, preset, en, reset
  D_Flip_Flop d_ff_5 (
    .clk(or_1_out), .D(d_ff_5_qn), .Q(d_ff_5_q), .Qn(d_ff_5_qn), .reset(not_6_out));  // open: preset, en
  Multiplexer #(.disabled(0), .enable("false")) multiplexer_2 (
    .in0(dataIn[1]), .in1(d_ff_4_q), .out(multiplexer_2_out), .sel(d_ff_2_q));
  D_Flip_Flop d_ff_6 (.clk(or_1_out), .D(multiplexer_2_out), .Q(d_ff_6_q));  // open: Qn, preset, en, reset
  xor xor_1 (xor_1_out, d_ff_8_q, d_ff_5_q);
  Multiplexer #(.disabled(0), .enable("false")) multiplexer_3 (
    .in0(dataIn[2]), .in1(d_ff_6_q), .out(multiplexer_3_out), .sel(d_ff_2_q));
  D_Flip_Flop d_ff_7 (.clk(or_1_out), .D(multiplexer_3_out), .Q(d_ff_7_q));  // open: Qn, preset, en, reset
  and and_2 (and_2_out, d_ff_5_q, d_ff_8_q);
  xor xor_2 (xor_2_out, and_2_out, d_ff_11_q);
  D_Flip_Flop d_ff_8 (.clk(or_1_out), .D(xor_1_out), .Q(d_ff_8_q), .reset(not_6_out));  // open: Qn, preset, en
  Multiplexer #(.disabled(0), .enable("false")) multiplexer_4 (
    .in0(dataIn[3]), .in1(d_ff_7_q), .out(multiplexer_4_out), .sel(d_ff_2_q));
  D_Flip_Flop d_ff_9 (.clk(or_1_out), .D(multiplexer_4_out), .Q(d_ff_9_q));  // open: Qn, preset, en, reset
  and and_3 (and_3_out, d_ff_5_q, d_ff_8_q, d_ff_11_q);
  Multiplexer #(.disabled(0), .enable("false")) multiplexer_5 (
    .in0(dataIn[4]), .in1(d_ff_9_q), .out(multiplexer_5_out), .sel(d_ff_2_q));
  D_Flip_Flop d_ff_10 (
    .clk(or_1_out), .D(multiplexer_5_out), .Q(d_ff_10_q), .reset(not_7_out));  // open: Qn, preset, en
  not not_7 (not_7_out, not_1_out);
  xor xor_3 (xor_3_out, and_3_out, d_ff_13_q);
  D_Flip_Flop d_ff_11 (.clk(or_1_out), .D(xor_2_out), .Q(d_ff_11_q), .reset(not_6_out));  // open: Qn, preset, en
  Multiplexer #(.disabled(0), .enable("false")) multiplexer_6 (
    .in0(dataIn[5]), .in1(d_ff_10_q), .out(multiplexer_6_out), .sel(d_ff_2_q));
  D_Flip_Flop d_ff_12 (
    .clk(or_1_out), .D(multiplexer_6_out), .Q(d_ff_12_q), .reset(not_8_out));  // open: Qn, preset, en
  not not_8 (not_8_out, not_1_out);
  D_Flip_Flop d_ff_13 (.clk(or_1_out), .D(xor_3_out), .Q(d_ff_13_q), .reset(not_6_out));  // open: Qn, preset, en
  Multiplexer #(.disabled(0), .enable("false")) multiplexer_7 (
    .in0(dataIn[6]), .in1(d_ff_12_q), .out(multiplexer_7_out), .sel(d_ff_2_q));
  D_Flip_Flop d_ff_14 (
    .clk(or_1_out), .D(multiplexer_7_out), .Q(d_ff_14_q), .reset(not_9_out));  // open: Qn, preset, en
  not not_9 (not_9_out, not_1_out);
  Multiplexer #(.disabled(0), .enable("false")) multiplexer_8 (
    .in0(dataIn[7]), .in1(d_ff_14_q), .out(multiplexer_8_out), .sel(d_ff_2_q));
  D_Flip_Flop d_ff_15 (
    .clk(or_1_out), .D(multiplexer_8_out), .Q(d_ff_15_q), .reset(not_10_out));  // open: Qn, preset, en
  not not_10 (not_10_out, not_1_out);
  D_Flip_Flop d_ff_16 (.clk(or_1_out), .D(d_ff_15_q), .Q(out_4), .preset(not_11_out));  // open: Qn, en, reset
  not not_11 (not_11_out, not_1_out);

  // Notes on the sheet:
  //   74HC166
  //   74HC161
  //   74HC161
endmodule

module SPI (
  input  [7:0] dataIn,
  input  Latch_Shift,
  input  LatchClk,
  input  MISO,
  input  nReset,
  input  clk,
  input  Start,
  input  [1:0] Mode,
  output MOSI,
  output [7:0] out_10,
  output Done,
  output clkOut
);

  wire and_1_out, and_2_out, and_3_out, clock_1_out, d_ff_1_q, d_ff_2_q, d_ff_4_qn, d_ff_5_q, d_ff_7_qn,
       d_ff_9_qn, d_ff_11_qn, multiplexer_1_out, multiplexer_2_out, multiplexer_3_out, multiplexer_4_out,
       multiplexer_5_out, multiplexer_6_out, multiplexer_7_out, multiplexer_8_out, not_1_out, not_2_out,
       not_3_out, not_4_out, not_5_out, not_6_out, not_7_out, not_8_out, not_9_out;

  not not_1 (not_1_out, Latch_Shift);
  not not_2 (not_2_out, nReset);
  Clock clock_1 (.out(clock_1_out));
  and and_1 (and_1_out, LatchClk, not_3_out);
  not not_3 (not_3_out, and_3_out);
  not not_4 (not_4_out, Start);
  D_Flip_Flop d_ff_1 (.clk(and_3_out), .D(MOSI), .Q(d_ff_1_q), .reset(not_2_out));  // open: Qn, preset, en
  D_Flip_Flop d_ff_2 (.clk(clock_1_out), .D(1'b1), .Q(d_ff_2_q), .reset(not_5_out));  // open: Qn, preset, en
  not not_5 (not_5_out, not_4_out);
  Multiplexer #(.disabled(0), .enable("false")) multiplexer_1 (
    .in0(dataIn[0]), .in1(d_ff_1_q), .out(multiplexer_1_out), .sel(not_1_out));
  D_Flip_Flop d_ff_3 (
    .clk(and_1_out), .D(multiplexer_1_out), .Q(out_10[0]), .reset(not_2_out));  // open: Qn, preset, en
  D_Flip_Flop d_ff_4 (.clk(and_3_out), .D(d_ff_4_qn), .Qn(d_ff_4_qn), .reset(not_6_out));  // open: Q, preset, en
  not not_6 (not_6_out, not_4_out);
  not not_7 (not_7_out, clock_1_out);
  and and_2 (and_2_out, not_7_out, d_ff_5_q);
  D_Flip_Flop d_ff_5 (.clk(clock_1_out), .D(d_ff_2_q), .Q(d_ff_5_q), .reset(not_9_out));  // open: Qn, preset, en
  not not_8 (not_8_out, Done);
  not not_9 (not_9_out, not_4_out);
  Multiplexer #(.disabled(0), .enable("false")) multiplexer_2 (
    .in0(dataIn[1]), .in1(out_10[0]), .out(multiplexer_2_out), .sel(not_1_out));
  D_Flip_Flop d_ff_6 (
    .clk(and_1_out), .D(multiplexer_2_out), .Q(out_10[1]), .reset(not_2_out));  // open: Qn, preset, en
  D_Flip_Flop d_ff_7 (.clk(d_ff_4_qn), .D(d_ff_7_qn), .Qn(d_ff_7_qn), .reset(not_6_out));  // open: Q, preset, en
  and and_3 (and_3_out, and_2_out, not_8_out);
  Multiplexer #(.disabled(0), .enable("false")) multiplexer_3 (
    .in0(dataIn[2]), .in1(out_10[1]), .out(multiplexer_3_out), .sel(not_1_out));
  D_Flip_Flop d_ff_8 (
    .clk(and_1_out), .D(multiplexer_3_out), .Q(out_10[2]), .reset(not_2_out));  // open: Qn, preset, en
  D_Flip_Flop d_ff_9 (.clk(d_ff_7_qn), .D(d_ff_9_qn), .Qn(d_ff_9_qn), .reset(not_6_out));  // open: Q, preset, en
  xor xor_1 (clkOut, and_3_out, Mode[1]);
  Multiplexer #(.disabled(0), .enable("false")) multiplexer_4 (
    .in0(dataIn[3]), .in1(out_10[2]), .out(multiplexer_4_out), .sel(not_1_out));
  D_Flip_Flop d_ff_10 (
    .clk(and_1_out), .D(multiplexer_4_out), .Q(out_10[3]), .reset(not_2_out));  // open: Qn, preset, en
  D_Flip_Flop d_ff_11 (
    .clk(d_ff_9_qn), .D(d_ff_11_qn), .Q(Done), .Qn(d_ff_11_qn), .reset(not_6_out));  // open: preset, en
  Multiplexer #(.disabled(0), .enable("false")) multiplexer_5 (
    .in0(dataIn[4]), .in1(out_10[3]), .out(multiplexer_5_out), .sel(not_1_out));
  D_Flip_Flop d_ff_12 (
    .clk(and_1_out), .D(multiplexer_5_out), .Q(out_10[4]), .reset(not_2_out));  // open: Qn, preset, en
  Multiplexer #(.disabled(0), .enable("false")) multiplexer_6 (
    .in0(dataIn[5]), .in1(out_10[4]), .out(multiplexer_6_out), .sel(not_1_out));
  D_Flip_Flop d_ff_13 (
    .clk(and_1_out), .D(multiplexer_6_out), .Q(out_10[5]), .reset(not_2_out));  // open: Qn, preset, en
  Multiplexer #(.disabled(0), .enable("false")) multiplexer_7 (
    .in0(dataIn[6]), .in1(out_10[5]), .out(multiplexer_7_out), .sel(not_1_out));
  D_Flip_Flop d_ff_14 (
    .clk(and_1_out), .D(multiplexer_7_out), .Q(out_10[6]), .reset(not_2_out));  // open: Qn, preset, en
  Multiplexer #(.disabled(0), .enable("false")) multiplexer_8 (
    .in0(dataIn[7]), .in1(out_10[6]), .out(multiplexer_8_out), .sel(not_1_out));
  D_Flip_Flop d_ff_15 (.clk(and_1_out), .D(multiplexer_8_out), .Q(MOSI), .reset(not_2_out));  // open: Qn, preset, en

  assign out_10[7] = MOSI;

  // Notes on the sheet:
  //   74HC161
  //   74HC166
endmodule

module _3StateLatch8 (
  input  [7:0] in_1,
  input  in_2,
  output [7:0] out_3
);


  assign out_3 = in_1;
endmodule
