// Logisim project SUB__ADD.circ as structural Verilog: 16 circuits, main circuit SUB1
module SUB1 (
  input  u,
  input  A,
  input  B,
  output Y,
  output r
);

  wire nand_1_out, nand_2_out, nand_3_out, nand_4_out, nand_5_out, nand_6_out, nand_7_out, not_1_out,
       not_2_out, not_3_out;

  not not_1 (not_1_out, u);
  not not_2 (not_2_out, A);
  not not_3 (not_3_out, B);
  nand nand_1 (nand_1_out, not_1_out, not_2_out, not_3_out);
  nand nand_2 (nand_2_out, not_1_out, A, B);
  nand nand_3 (nand_3_out, u, not_2_out, B);
  nand nand_4 (nand_4_out, u, A, not_3_out);
  nand nand_5 (nand_5_out, A, not_3_out);
  nand nand_6 (nand_6_out, u, not_3_out);
  nand nand_7 (nand_7_out, u, A);
  nand nand_8 (Y, nand_1_out, nand_2_out, nand_3_out, nand_4_out);
  nand nand_9 (r, nand_5_out, nand_6_out, nand_7_out);
endmodule

module SUB1_B (
  input  u,
  input  A,
  input  B,
  output Y,
  output r
);

  wire and_1_out, and_2_out, and_3_out, and_4_out, and_5_out, and_6_out, and_7_out, not_1_out, not_2_out,
       not_3_out;

  not not_1 (not_1_out, u);
  not not_2 (not_2_out, A);
  not not_3 (not_3_out, B);
  and and_1 (and_1_out, not_1_out, not_2_out, not_3_out);
  and and_2 (and_2_out, not_1_out, A, B);
  and and_3 (and_3_out, u, not_2_out, B);
  and and_4 (and_4_out, u, A, not_3_out);
  and and_5 (and_5_out, A, not_3_out);
  and and_6 (and_6_out, u, not_3_out);
  and and_7 (and_7_out, u, A);
  or or_1 (Y, and_1_out, and_2_out, and_3_out, and_4_out);
  or or_2 (r, and_5_out, and_6_out, and_7_out);
endmodule

module _8Bit_SUB (
  input  [7:0] A,
  input  [7:0] B,
  output [7:0] Y
);

  wire sub1_1_r, sub1_2_r, sub1_3_r, sub1_4_r, sub1_5_r, sub1_6_r, sub1_7_r, sub1_8_r;

  SUB1 sub1_1 (.u(1'b1), .A(A[0]), .B(B[0]), .Y(Y[0]), .r(sub1_1_r));
  SUB1 sub1_2 (.u(sub1_1_r), .A(A[1]), .B(B[1]), .Y(Y[1]), .r(sub1_2_r));
  SUB1 sub1_3 (.u(sub1_2_r), .A(A[2]), .B(B[2]), .Y(Y[2]), .r(sub1_3_r));
  SUB1 sub1_4 (.u(sub1_3_r), .A(A[3]), .B(B[3]), .Y(Y[3]), .r(sub1_4_r));
  SUB1 sub1_5 (.u(sub1_4_r), .A(A[4]), .B(B[4]), .Y(Y[4]), .r(sub1_5_r));
  SUB1 sub1_6 (.u(sub1_5_r), .A(A[5]), .B(B[5]), .Y(Y[5]), .r(sub1_6_r));
  SUB1 sub1_7 (.u(sub1_6_r), .A(A[6]), .B(B[6]), .Y(Y[6]), .r(sub1_7_r));
  SUB1 sub1_8 (.u(sub1_7_r), .A(A[7]), .B(B[7]), .Y(Y[7]), .r(sub1_8_r));
endmodule

module SUB_From0 (
  input  u,
  input  B,
  output Y,
  output r
);

  wire and_1_out, and_2_out, not_1_out, not_2_out, not_3_out;

  not not_1 (not_1_out, u);
  not not_2 (not_2_out, B);
  not not_3 (not_3_out, B);
  and and_1 (and_1_out, not_1_out, not_2_out);
  and and_2 (and_2_out, u, B);
  and and_3 (r, u, not_3_out);
  or or_1 (Y, and_1_out, and_2_out);
endmodule

module Selector (
  input  S,
  input  A,
  input  B,
  output Y
);

  wire and_1_out, and_2_out, not_1_out;

  not not_1 (not_1_out, S);
  and and_1 (and_1_out, not_1_out, A);
  and and_2 (and_2_out, S, B);
  or or_1 (Y, and_1_out, and_2_out);
endmodule

module SUB_ADD1 (
  input  u,
  input  A,
  input  B,
  input  OP,
  output Y,
  output r
);

  wire and_1_out, and_2_out, and_3_out, and_4_out, and_5_out, and_6_out, and_7_out, and_8_out, and_9_out,
       not_1_out, not_2_out, not_3_out, not_4_out, not_5_out, or_1_out;

  and and_1 (and_1_out, B, OP);
  not not_1 (not_1_out, B);
  and and_2 (and_2_out, not_1_out, not_2_out);
  not not_2 (not_2_out, OP);
  or or_1 (or_1_out, and_1_out, and_2_out);
  not not_3 (not_3_out, u);
  not not_4 (not_4_out, A);
  not not_5 (not_5_out, or_1_out);
  and and_3 (and_3_out, not_3_out, not_4_out, not_5_out);
  and and_4 (and_4_out, not_3_out, A, or_1_out);
  or or_2 (Y, and_3_out, and_4_out, and_5_out, and_6_out);
  and and_5 (and_5_out, u, not_4_out, or_1_out);
  and and_6 (and_6_out, u, A, not_5_out);
  and and_7 (and_7_out, A, not_5_out);
  or or_3 (r, and_7_out, and_8_out, and_9_out);
  and and_8 (and_8_out, u, not_5_out);
  and and_9 (and_9_out, u, A);

  // Notes on the sheet:
  //   0:ADD 1:SUB
endmodule

module Selector_4Input (
  input  S1,
  input  S0,
  input  A,
  input  B,
  input  C,
  input  D,
  output Y
);

  wire and_1_out, and_2_out, and_3_out, and_4_out, not_1_out, not_2_out, not_3_out, not_4_out;

  not not_1 (not_1_out, S1);
  not not_2 (not_2_out, S0);
  not not_3 (not_3_out, S1);
  not not_4 (not_4_out, S0);
  and and_1 (and_1_out, not_1_out, not_2_out, A);
  and and_2 (and_2_out, not_3_out, S0, B);
  and and_3 (and_3_out, S1, not_4_out, C);
  and and_4 (and_4_out, S1, S0, D);
  or or_1 (Y, and_1_out, and_2_out, and_3_out, and_4_out);
endmodule

module SUB_BCD (
  input  u,
  input  A,
  input  B,
  output Y,
  output r2
);

  wire xor_1_out;

  xor xor_1 (xor_1_out, u, A, B);
  not not_1 (Y, xor_1_out);
  ROM #(.addrWidth(3), .dataWidth(1)) rom_1 (.addr({B, A, u}), .data(r2));  // open: sel

  // Notes on the sheet:
  //   contents of rom_1 (hex, n*v repeats v):
  //   0 1 1 1 0 0 0 1
endmodule

module upcounter (
  input  E,
  input  clk
);

  wire and_1_out, and_2_out, and_3_out, d_ff_1_q, d_ff_2_q, d_ff_3_q, d_ff_4_q, xor_1_out, xor_2_out,
       xor_3_out, xor_4_out;

  and and_1 (and_1_out, d_ff_1_q, E);
  and and_2 (and_2_out, and_1_out, d_ff_2_q);
  and and_3 (and_3_out, and_2_out, d_ff_3_q);
  xor xor_1 (xor_1_out, d_ff_1_q, E);
  xor xor_2 (xor_2_out, d_ff_2_q, and_1_out);
  xor xor_3 (xor_3_out, d_ff_3_q, and_2_out);
  xor xor_4 (xor_4_out, d_ff_4_q, and_3_out);
  D_Flip_Flop d_ff_1 (.clk(clk), .D(xor_1_out), .Q(d_ff_1_q));  // open: Qn, preset, en, reset
  D_Flip_Flop d_ff_2 (.clk(clk), .D(xor_2_out), .Q(d_ff_2_q));  // open: Qn, preset, en, reset
  D_Flip_Flop d_ff_3 (.clk(clk), .D(xor_3_out), .Q(d_ff_3_q));  // open: Qn, preset, en, reset
  D_Flip_Flop d_ff_4 (.clk(clk), .D(xor_4_out), .Q(d_ff_4_q));  // open: Qn, preset, en, reset
endmodule

module FullAdder (
  input  B,
  input  A,
  input  CIn,
  output P,
  output Y,
  output COut,
  output G
);

  wire and_1_out;

  xor xor_1 (P, B, A);
  xor xor_2 (Y, P, CIn);
  and and_1 (and_1_out, P, CIn);
  and and_2 (G, B, A);
  or or_1 (COut, and_1_out, G);
endmodule

module Prefix (
  input  Gi,
  input  Pi,
  input  Gj,
  input  Pj,
  output G_1,
  output P_1
);

  wire and_1_out;

  and and_1 (and_1_out, Gi, Pj);
  and and_2 (P_1, Pi, Pj);
  or or_1 (G_1, and_1_out, Gj);
endmodule

module PrefixWC (
  input  Cin,
  input  Gi,
  input  Pi,
  input  Gj,
  input  Pj,
  output G_1,
  output P_1
);

  wire and_1_out, and_2_out, or_1_out;

  and and_1 (and_1_out, Cin, Pi);
  or or_1 (or_1_out, and_1_out, Gi);
  and and_2 (and_2_out, or_1_out, Pj);
  and and_3 (P_1, Pi, Pj);
  or or_2 (G_1, and_2_out, Gj);
endmodule

module SUBADD_B (
  input  u,
  input  A,
  input  B,
  input  OP,
  output Y,
  output r
);

  wire and_1_out, and_2_out, and_3_out, and_4_out, and_5_out, and_6_out, and_7_out, not_1_out, not_2_out,
       not_3_out, xor_1_out;

  xor xor_1 (xor_1_out, B, OP);
  not not_1 (not_1_out, u);
  not not_2 (not_2_out, A);
  not not_3 (not_3_out, xor_1_out);
  and and_1 (and_1_out, not_1_out, not_2_out, not_3_out);
  and and_2 (and_2_out, not_1_out, A, xor_1_out);
  or or_1 (Y, and_1_out, and_2_out, and_3_out, and_4_out);
  and and_3 (and_3_out, u, not_2_out, xor_1_out);
  and and_4 (and_4_out, u, A, not_3_out);
  and and_5 (and_5_out, A, not_3_out);
  or or_2 (r, and_5_out, and_6_out, and_7_out);
  and and_6 (and_6_out, u, not_3_out);
  and and_7 (and_7_out, u, A);

  // Notes on the sheet:
  //   0:SUB 1:ADD
endmodule

module ADDSUB_XOR (
  input  A3,
  input  B3,
  input  A2,
  input  B2,
  input  A1,
  input  B1,
  input  A0,
  input  B0,
  input  Cin,
  output Cout,
  output S3,
  output S2,
  output S1,
  output S0
);

  wire and_1_out, and_2_out, and_3_out, and_4_out, and_5_out, and_6_out, and_7_out, and_8_out, and_9_out,
       and_10_out, and_11_out, and_12_out, and_13_out, and_14_out, or_1_out, or_2_out, or_3_out, xor_1_out,
       xor_2_out, xor_3_out, xor_4_out;

  and and_1 (and_1_out, A3, B3);
  xor xor_1 (xor_1_out, A3, B3);
  and and_2 (and_2_out, A2, B2);
  xor xor_2 (xor_2_out, A2, B2);
  and and_3 (and_3_out, A1, B1);
  xor xor_3 (xor_3_out, A1, B1);
  and and_4 (and_4_out, A0, B0);
  xor xor_4 (xor_4_out, A0, B0);
  and and_5 (and_5_out, and_2_out, xor_1_out);
  and and_6 (and_6_out, xor_1_out, xor_2_out, and_3_out);
  and and_7 (and_7_out, xor_1_out, xor_2_out, xor_3_out, and_4_out);
  and and_8 (and_8_out, xor_1_out, xor_2_out, xor_3_out, xor_4_out, Cin);
  and and_9 (and_9_out, xor_2_out, and_3_out);
  and and_10 (and_10_out, xor_2_out, xor_3_out, and_4_out);
  and and_11 (and_11_out, xor_2_out, xor_3_out, xor_4_out, Cin);
  and and_12 (and_12_out, xor_3_out, and_4_out);
  and and_13 (and_13_out, xor_3_out, xor_4_out, Cin);
  and and_14 (and_14_out, xor_4_out, Cin);
  or or_1 (or_1_out, and_2_out, and_9_out, and_10_out, and_11_out);
  or or_2 (or_2_out, and_3_out, and_12_out, and_13_out);
  or or_3 (or_3_out, and_4_out, and_14_out);
  or or_4 (Cout, and_1_out, and_5_out, and_6_out, and_7_out, and_8_out);
  xor xor_5 (S3, xor_1_out, or_1_out);
  xor xor_6 (S2, xor_2_out, or_2_out);
  xor xor_7 (S1, xor_3_out, or_3_out);
  xor xor_8 (S0, xor_4_out, Cin);
endmodule

module sub_add_half (
  input  A,
  input  A_2,
  input  B,
  input  B_2,
  input  CarryIn,
  input  A_3,
  input  B_3,
  input  BorrowIn,
  input  A_4,
  input  B_4,
  output Y,
  output Y_2,
  output Carry,
  output Borrow,
  output Y_3,
  output Carry_2,
  output Y_4,
  output Borrow_2
);

  wire and_2_out, and_3_out, and_4_out, and_5_out, xor_2_out, xor_3_out;

  xor xor_1 (Y, A, B);
  and and_1 (Carry, A, B);
  xor xor_2 (xor_2_out, A_3, B_3);
  and and_2 (and_2_out, A_3, B_3);
  xor xor_3 (xor_3_out, A_4, B_4);
  and and_3 (and_3_out, ~A_4, B_4);  // AND_Gate
  xor xor_4 (Y_3, CarryIn, xor_2_out);
  and and_4 (and_4_out, xor_2_out, CarryIn);
  or or_1 (Carry_2, and_4_out, and_2_out);
  xor xor_5 (Y_4, BorrowIn, xor_3_out);
  and and_5 (and_5_out, ~xor_3_out, BorrowIn);  // AND_Gate
  or or_2 (Borrow_2, and_5_out, and_3_out);
  xor xor_6 (Y_2, A_2, B_2);
  and and_6 (Borrow, ~A_2, B_2);  // AND_Gate

  // Notes on the sheet:
  //   Half adder
  //   Half subtractor 
endmodule

module sub_full (
  input  A,
  input  u,
  input  B,
  output r,
  output r_2,
  output Y,
  output Y_2,
  output \ｒ ,
  output Y_3
);

  wire and_1_out, and_2_out, and_3_out, and_4_out, and_5_out, and_6_out, and_7_out, and_8_out, and_9_out,
       and_10_out, and_11_out, and_12_out, not_1_out, not_2_out, not_3_out, xor_1_out, xor_2_out, xor_4_out,
       xor_5_out;

  not not_1 (not_1_out, A);
  not not_2 (not_2_out, u);
  not not_3 (not_3_out, B);
  xor xor_1 (xor_1_out, u, B);
  and and_1 (and_1_out, not_1_out, u, not_3_out);
  and and_2 (and_2_out, A, not_2_out, not_3_out);
  and and_3 (and_3_out, A, u, not_3_out);
  and and_4 (and_4_out, A, u, B);
  and and_5 (and_5_out, not_1_out, not_2_out, not_3_out);
  and and_6 (and_6_out, not_1_out, u, B);
  and and_7 (and_7_out, A, not_2_out, B);
  and and_8 (and_8_out, A, u, not_3_out);
  xor xor_2 (xor_2_out, A, u);
  and and_9 (and_9_out, xor_2_out, ~B);  // AND_Gate
  and and_10 (and_10_out, A, u);
  xor xor_3 (Y_3, xor_1_out, ~A);  // XOR_Gate
  or or_1 (r_2, and_1_out, and_2_out, and_3_out, and_4_out);
  or or_2 (Y_2, and_5_out, and_6_out, and_7_out, and_8_out);
  or or_3 (\ｒ , and_9_out, and_10_out);
  and and_11 (and_11_out, A, u);
  xor xor_4 (xor_4_out, A, u);
  or or_4 (r, and_11_out, and_12_out);
  and and_12 (and_12_out, xor_4_out, ~B);  // AND_Gate
  xor xor_5 (xor_5_out, u, B);
  xor xor_6 (Y, xor_5_out, ~A);  // XOR_Gate
endmodule
